// Logisim project s-mips.circ as structural Verilog: 19 circuits, main circuit S-MIPS Board
module S_MIPS_Board (
  output halt
);

  wire button_1_out, CLK, CS, d_ff_1_q, R_W, Reset_out, RST, TTY_EN;
  wire [2:0] KDB;
  wire [3:0] Mask, ram_1_read_time, ram_1_write_time;
  wire [6:0] KDB_DATA, TTY_DATA;
  wire [15:0] Addr;
  wire [31:0] ram_1_data_out_0, ram_1_data_out_1, ram_1_data_out_2, ram_1_data_out_3, s_mips_1_ram_in_0,
       s_mips_1_ram_in_1, s_mips_1_ram_in_2, s_mips_1_ram_in_3;

  TTY #(.rows(25), .cols(80)) tty_1 (.data(TTY_DATA), .clk(CLK), .we(TTY_EN), .clr(RST));
  RAM ram_1 (
    .Address(Addr), .Data_Out_0(ram_1_data_out_0), .Data_Out_1(ram_1_data_out_1),
    .Data_Out_2(ram_1_data_out_2), .Data_Out_3(ram_1_data_out_3), .Data_In_0(s_mips_1_ram_in_0),
    .Data_In_1(s_mips_1_ram_in_1), .Data_In_2(s_mips_1_ram_in_2), .Data_In_3(s_mips_1_ram_in_3), .Mask(Mask),
    .nRead_Write(R_W), .Chip_Select(CS), .Read_Time(ram_1_read_time), .Reset(button_1_out),
    .Write_Time(ram_1_write_time));
  Button button_1 (.out(button_1_out));
  Keyboard #(.buflen(64)) keyboard_1 (.clk(CLK), .re(KDB[0]), .avail(KDB[2]), .data(KDB_DATA));  // open: clr
  S_MIPS s_mips_1 (
    .Kbd_Enable(KDB[0]), .Address(Addr), .Kbd_Clear(KDB[1]), .Kbd_Available(KDB[2]),
    .RAM_In_0(s_mips_1_ram_in_0), .Kbd_ASCII_Data(KDB_DATA), .RAM_In_1(s_mips_1_ram_in_1),
    .TTY_Enable(TTY_EN), .RAM_In_2(s_mips_1_ram_in_2), .RAM_In_3(s_mips_1_ram_in_3),
    .TTY_ASCII_Data(TTY_DATA), .Reset(RST), .RAM_Out_0(ram_1_data_out_0), .Clock(CLK),
    .RAM_Out_1(ram_1_data_out_1), .Stop(halt), .RAM_Out_2(ram_1_data_out_2), .RAM_Out_3(ram_1_data_out_3),
    .Mask(Mask), .Read_Time(ram_1_read_time), .Write_Time(ram_1_write_time), .nRead_Write(R_W),
    .Chip_Select(CS));
  D_Flip_Flop d_ff_1 (.clk(CLK), .D(1'b1), .Q(d_ff_1_q), .reset(Reset_out));  // open: Qn, preset, en
  Button Reset (.out(Reset_out));
  Clock clock_1 (.out(CLK));
  D_Flip_Flop d_ff_2 (.clk(CLK), .D(d_ff_1_q), .Qn(RST), .reset(Reset_out));  // open: Q, preset, en

  // Notes on the sheet:
  //   NO MODIFICAR
  //   Keyboard
endmodule

module RAM (
  input  [15:0] Address,
  input  [31:0] Data_In_0,
  input  [31:0] Data_In_1,
  input  [31:0] Data_In_2,
  input  [31:0] Data_In_3,
  input  [3:0] Mask,
  input  nRead_Write,
  input  Chip_Select,
  input  Reset,
  output [31:0] Data_Out_0,
  output [31:0] Data_Out_1,
  output [31:0] Data_Out_2,
  output [31:0] Data_Out_3,
  output [3:0] Read_Time,
  output [3:0] Write_Time
);

  wire and_2_out, and_3_out, and_4_out, and_5_out, and_6_out, and_7_out, and_8_out, and_9_out, Changed, CLK,
       comparator_2_eq, comparator_3_eq, comparator_4_eq, comparator_5_eq, comparator_6_eq, Count,
       demultiplexer_3_out0, Idle, Idle_q, Load, Load0, Load1, nand_1_out, or_1_out, or_2_out, or_3_out,
       or_4_out, or_5_out, or_6_out, or_7_out, or_8_out, or_9_out, or_10_out, Proc_q, Update_Mem, Zero_Time;
  wire [3:0] counter_1_q, multiplexer_1_out, subtractor_1_out;
  wire [31:0] register_1_q, register_2_q, register_3_q, register_4_q, register_5_q;

  // Probe on 4'b0011
  // Probe on 4'b0101
  Multiplexer #(.width(4), .enable("false")) multiplexer_1 (
    .in0(4'b0011), .in1(4'b0101), .out(multiplexer_1_out), .sel(nRead_Write));
  or or_1 (or_1_out, Idle, Update_Mem);
  or or_2 (or_2_out, ~Chip_Select, Reset);  // OR_Gate
  Subtractor #(.width(4)) subtractor_1 (.a(multiplexer_1_out), .b(4'b0010), .out(subtractor_1_out));  // open: bin, bout
  D_Flip_Flop u_Idle (.clk(CLK), .D(or_1_out), .Q(Idle_q), .preset(or_2_out));  // open: Qn, en, reset
  Demultiplexer #(.enable("false")) demultiplexer_1 (.out0(Idle), .out1(Load0), .in(Idle_q), .sel(Changed));
  // Probe on counter_1_q
  Counter #(.width(4), .max('hf)) counter_1 (
    .load(Load), .D(subtractor_1_out), .count(Count), .Q(counter_1_q), .clk(CLK), .clr(or_3_out));  // open: carry
  or or_3 (or_3_out, ~Chip_Select, Reset);  // OR_Gate
  Comparator #(.width(4), .mode("unsigned")) comparator_1 (
    .a(4'b0000), .b(counter_1_q), .eq(Zero_Time));  // open: gt, lt
  or or_4 (or_4_out, Count, Load0, Load1);
  Register #(.width(32)) register_1 (.D(Data_In_0), .en(Chip_Select), .Q(register_1_q), .clk(CLK), .clr(or_5_out));
  or or_5 (or_5_out, ~Chip_Select, Reset);  // OR_Gate
  Register #(.width(32)) register_2 (.D(Data_In_1), .en(Chip_Select), .Q(register_2_q), .clk(CLK), .clr(or_6_out));
  or or_6 (or_6_out, ~Chip_Select, Reset);  // OR_Gate
  Register #(.width(32)) register_3 (.D(Data_In_2), .en(Chip_Select), .Q(register_3_q), .clk(CLK), .clr(or_7_out));
  or or_7 (or_7_out, ~Chip_Select, Reset);  // OR_Gate
  Register #(.width(32)) register_4 (.D(Data_In_3), .en(Chip_Select), .Q(register_4_q), .clk(CLK), .clr(or_8_out));
  or or_8 (or_8_out, ~Chip_Select, Reset);  // OR_Gate
  Register #(.width(32)) register_5 (
    .D({{11{1'b1}}, nRead_Write, Mask, Address}), .en(Chip_Select), .Q(register_5_q), .clk(CLK),
    .clr(or_9_out));
  or or_9 (or_9_out, ~Chip_Select, Reset);  // OR_Gate
  D_Flip_Flop Proc (.clk(CLK), .D(or_4_out), .Q(Proc_q), .reset(or_10_out));  // open: Qn, preset, en
  or or_10 (or_10_out, ~Chip_Select, Reset);  // OR_Gate
  Demultiplexer #(.enable("false")) demultiplexer_2 (
    .out0(Count), .out1(Update_Mem), .in(demultiplexer_3_out0), .sel(Zero_Time));
  Demultiplexer #(.enable("false")) demultiplexer_3 (
    .out0(demultiplexer_3_out0), .out1(Load1), .in(Proc_q), .sel(Changed));
  Clock clock_1 (.out(CLK));
  Comparator #(.width(32)) comparator_2 (.a(register_1_q), .b(Data_In_0), .eq(comparator_2_eq));  // open: gt, lt
  Comparator #(.width(32)) comparator_3 (.a(register_2_q), .b(Data_In_1), .eq(comparator_3_eq));  // open: gt, lt
  Comparator #(.width(32)) comparator_4 (.a(register_3_q), .b(Data_In_2), .eq(comparator_4_eq));  // open: gt, lt
  Comparator #(.width(32)) comparator_5 (.a(register_4_q), .b(Data_In_3), .eq(comparator_5_eq));  // open: gt, lt
  Comparator #(.width(32)) comparator_6 (
    .a(register_5_q), .b({{11{1'b1}}, nRead_Write, Mask, Address}), .eq(comparator_6_eq));  // open: gt, lt
  nand nand_1 (nand_1_out, comparator_6_eq, comparator_2_eq, comparator_3_eq, comparator_4_eq, comparator_5_eq);
  and and_1 (Changed, nand_1_out, Chip_Select);
  or or_11 (Load, Count, Load1, Load0);
  and and_2 (and_2_out, Mask[0], Update_Mem, nRead_Write);
  and and_3 (and_3_out, Mask[1], Update_Mem, nRead_Write);
  and and_4 (and_4_out, Mask[2], Update_Mem, nRead_Write);
  and and_5 (and_5_out, Mask[3], Update_Mem, nRead_Write);
  RAM_part #(.addrWidth(16), .dataWidth(32), .bus("separate")) ram_1 (
    .addr(Address), .din(Data_In_0), .data(Data_Out_0), .str(and_2_out), .sel(Chip_Select), .clk(CLK),
    .ld(and_6_out), .clr(Reset));
  and and_6 (and_6_out, ~nRead_Write, Idle);  // AND_Gate
  RAM_part #(.addrWidth(16), .dataWidth(32), .bus("separate")) ram_2 (
    .addr(Address), .din(Data_In_1), .data(Data_Out_1), .str(and_3_out), .sel(Chip_Select), .clk(CLK),
    .ld(and_7_out), .clr(Reset));
  and and_7 (and_7_out, ~nRead_Write, Idle);  // AND_Gate
  RAM_part #(.addrWidth(16), .dataWidth(32), .bus("separate")) ram_3 (
    .addr(Address), .din(Data_In_2), .data(Data_Out_2), .str(and_4_out), .sel(Chip_Select), .clk(CLK),
    .ld(and_8_out), .clr(Reset));
  and and_8 (and_8_out, ~nRead_Write, Idle);  // AND_Gate
  RAM_part #(.addrWidth(16), .dataWidth(32), .bus("separate")) ram_4 (
    .addr(Address), .din(Data_In_3), .data(Data_Out_3), .str(and_5_out), .sel(Chip_Select), .clk(CLK),
    .ld(and_9_out), .clr(Reset));
  and and_9 (and_9_out, ~nRead_Write, Idle);  // AND_Gate

  assign Read_Time = 4'b0011;
  assign Write_Time = 4'b0101;

  // Other names for the same wires on the sheet: M0 = Mask[0]; M1 = Mask[1]; M2 = Mask[2]; M3 = Mask[3];
  //   RW = nRead_Write; CLR = Reset; CS = Chip_Select; Load2 = Count

  // Notes on the sheet:
  //   NO MODIFICAR
  //   excepto quizás los valores RT y WT
  //   BANK0
  //   BANK1
  //   BANK2
  //   BANK3
endmodule

module S_MIPS (
  input  Kbd_Available,
  input  [6:0] Kbd_ASCII_Data,
  input  [31:0] RAM_Out_0,
  input  [31:0] RAM_Out_1,
  input  Reset,
  input  [31:0] RAM_Out_2,
  input  Clock,
  input  [31:0] RAM_Out_3,
  input  [3:0] Read_Time,
  input  [3:0] Write_Time,
  output Kbd_Enable,
  output [15:0] Address,
  output Kbd_Clear,
  output TTY_Enable,
  output [6:0] TTY_ASCII_Data,
  output Stop,
  output [31:0] RAM_In_0,
  output [31:0] RAM_In_1,
  output [31:0] RAM_In_2,
  output [31:0] RAM_In_3,
  output [3:0] Mask,
  output nRead_Write,
  output Chip_Select
);

  wire cache_CS, cache_RW, cacheEnd, controlunit_1_branch, controlunit_1_extop, controlunit_1_hilo_rw,
       controlunit_1_hilo_selector, controlunit_1_iord, controlunit_1_irwrite, controlunit_1_memread,
       controlunit_1_memwrite, controlunit_1_outa, controlunit_1_pcwrite, controlunit_1_regwrite, KBD_INPUT;
  wire [1:0] controlunit_1_alusrca, controlunit_1_alusrcb, controlunit_1_pcsrc, controlunit_1_regdst,
       controlunit_1_regwriteselector;
  wire [3:0] Cache_MASK;
  wire [5:0] controlunit_1_alucontrol, datapath_1_funccode, datapath_1_opcode;
  wire [15:0] RAM_C;
  wire [31:0] bit_extender_1_out, CPU_OUTPUT_0, CPU_OUTPUT_1, CPU_OUTPUT_2, CPU_OUTPUT_3,
       datapath_1_memoutputaddress, memoryoutputselection_1_output, multiplexer_1_out, multiplexer_2_out;
  wire [31:7] Ram_In;

  MemoryOutputSelection memoryoutputselection_1 (
    .Address(datapath_1_memoutputaddress), .Input_0(CPU_OUTPUT_0), .Input_1(CPU_OUTPUT_1),
    .Input_2(CPU_OUTPUT_2), .Input_3(CPU_OUTPUT_3), .Output(memoryoutputselection_1_output));
  Multiplexer #(.width(32), .enable("false")) multiplexer_1 (
    .in0({32{1'b1}}), .in1(bit_extender_1_out), .out(multiplexer_1_out), .sel(Kbd_Available));
  assign bit_extender_1_out = {{25{1'b0}}, Kbd_ASCII_Data};  // Bit_Extender bit_extender_1
  Cache cache_1 (
    .clk(Clock), .mask(Cache_MASK), .finish(cacheEnd), .read(Read_Time), .rst(Reset), .ramMask(Mask),
    .write(Write_Time), .address(RAM_C), .r_w(cache_RW), .cs(cache_CS), .Ram_address(Address),
    .rsmCS(Chip_Select), .ram_output0(RAM_Out_0), .ramR_W(nRead_Write),
    .cpu_input0({Ram_In, TTY_ASCII_Data}), .ram_output1(RAM_Out_1), .cpu_input1({Ram_In, TTY_ASCII_Data}),
    .ram_output2(RAM_Out_2), .cpu_input_2({Ram_In, TTY_ASCII_Data}), .ram_output3(RAM_Out_3),
    .cpu_input3({Ram_In, TTY_ASCII_Data}), .ram_input0(RAM_In_0), .cpu_output0(CPU_OUTPUT_0),
    .ram_input1(RAM_In_1), .cpu_output1(CPU_OUTPUT_1), .ram_input2(RAM_In_2), .cpu_output2(CPU_OUTPUT_2),
    .ram_input3(RAM_In_3), .cpu_output3(CPU_OUTPUT_3));
  Multiplexer #(.width(32), .enable("false")) multiplexer_2 (
    .in0(memoryoutputselection_1_output), .in1(multiplexer_1_out), .out(multiplexer_2_out), .sel(KBD_INPUT));
  ControlUnit controlunit_1 (
    .MemReadEnd(cacheEnd), .MemWriteEnd(cacheEnd), .OpCode(datapath_1_opcode),
    .FuncCode(datapath_1_funccode), .Reset(Reset), .Clock(Clock), .IorD(controlunit_1_iord),
    .RegDst(controlunit_1_regdst), .RegWriteSelector(controlunit_1_regwriteselector),
    .ALUSrcA(controlunit_1_alusrca), .ALUSrcB(controlunit_1_alusrcb), .Branch(controlunit_1_branch),
    .PCWrite(controlunit_1_pcwrite), .RegWrite(controlunit_1_regwrite), .PCSrc(controlunit_1_pcsrc),
    .ALUControl(controlunit_1_alucontrol), .IRWrite(controlunit_1_irwrite),
    .MemWrite(controlunit_1_memwrite), .MemRead(controlunit_1_memread), .ExtOp(controlunit_1_extop),
    .HiLo_RW(controlunit_1_hilo_rw), .HiLo_Selector(controlunit_1_hilo_selector), .OutA(controlunit_1_outa),
    .STOP(Stop), .TTY_ENABLE(TTY_Enable), .KBD_ENABLE(Kbd_Enable), .KBD_INPUT(KBD_INPUT));
  assign cache_RW = cache_CS ? controlunit_1_memwrite : 1'bz;  // Controlled_Buffer controlled_buffer_1
  or or_1 (cache_CS, controlunit_1_memwrite, controlunit_1_memread);
  // Probe on multiplexer_2_out
  DataPath datapath_1 (
    .Clock(Clock), .Reset(Reset), .Input(multiplexer_2_out), .IorD(controlunit_1_iord),
    .RegDst(controlunit_1_regdst), .RegWriteSelector(controlunit_1_regwriteselector),
    .ALUSrcA(controlunit_1_alusrca), .ALUSrcB(controlunit_1_alusrcb), .Branch(controlunit_1_branch),
    .PCWrite(controlunit_1_pcwrite), .RegWrite(controlunit_1_regwrite), .PCSrc(controlunit_1_pcsrc),
    .ALUControl(controlunit_1_alucontrol), .IRWrite(controlunit_1_irwrite), .ExtOp(controlunit_1_extop),
    .HiLo_RW(controlunit_1_hilo_rw), .HiLo_Selector(controlunit_1_hilo_selector), .OutA(controlunit_1_outa),
    .MemOutput({Ram_In, TTY_ASCII_Data}), .MemOutputAddress(datapath_1_memoutputaddress),
    .FuncCode(datapath_1_funccode), .OpCode(datapath_1_opcode));
  MemoryInputSelector memoryinputselector_1 (
    .Address(datapath_1_memoutputaddress), .Mask(Cache_MASK), .Address_2(RAM_C));
  // Probe on Cache_MASK
  // Probe on RAM_C

  // Other names for the same wires on the sheet: CLK = Clock; CLR = Reset; CS = Chip_Select;
  //   KBD_AVAIL = Kbd_Available; KBD_CLR = Kbd_Clear; KBD_DATA[6:0] = Kbd_ASCII_Data; RAM_A[15:0] = Address;
  //   Ram_In[6:0] = TTY_ASCII_Data; TTY_DATA[6:0] = TTY_ASCII_Data; RAM_INPUT_0[31:0] = RAM_In_0;
  //   RAM_INPUT_1[31:0] = RAM_In_1; RAM_INPUT_2[31:0] = RAM_In_2; RAM_INPUT_3[31:0] = RAM_In_3; RAM_MASK[3:0] = Mask;
  //   RAM_OUTPUT_0[31:0] = RAM_Out_0; RAM_OUTPUT_1[31:0] = RAM_Out_1; RAM_OUTPUT_2[31:0] = RAM_Out_2;
  //   RAM_OUTPUT_3[31:0] = RAM_Out_3; RW = nRead_Write

  // Notes on the sheet:
  //   RAM ADDRESS
  //   DATA FROM RAM
  //   DATA TO RAM
  //   DATA WRITE MASK
  //   RAM TIMING
  //   RAM CONTROL
  //   KEYBOARD
  //   TTY
  //   SEQUENCING
endmodule

module RegisterFile (
  input  [4:0] \Dirección_de_destino ,
  input  Read_Write,
  input  [31:0] Datos_de_entrada,
  input  [4:0] Selector_de_salida_A,
  input  [4:0] Selector_de_salida_B,
  input  Reset,
  input  Clock,
  output [31:0] Read_Data_1,
  output [31:0] Read_Data_2,
  output [31:0] SP
);

  wire or_1_out, Register_0_on_off, Register_1_on_off, Register_2_on_off, Register_3_on_off,
       Register_4_on_off, Register_5_on_off, Register_6_on_off, Register_7_on_off, Register_8_on_off,
       Register_9_on_off, Register_10_on_off, Register_11_on_off, Register_12_on_off, Register_13_on_off,
       Register_14_on_off, Register_15_on_off, Register_16_on_off, Register_17_on_off, Register_18_on_off,
       Register_19_on_off, Register_20_on_off, Register_21_on_off, Register_22_on_off, Register_23_on_off,
       Register_24_on_off, Register_25_on_off, Register_26_on_off, Register_27_on_off, Register_28_on_off,
       Register_29_on_off, Register_30_on_off, Register_31_on_off;
  wire [31:0] multiplexer_1_out, reg0_out, reg1_out, reg2_out, reg3_out, reg4_out, reg5_out, reg6_out,
       reg7_out, reg8_out, reg9_out, reg10_out, reg11_out, reg12_out, reg13_out, reg14_out, reg15_out,
       reg16_out, reg17_out, reg18_out, reg19_out, reg20_out, reg21_out, reg22_out, reg23_out, reg24_out,
       reg25_out, reg26_out, reg27_out, reg28_out, reg29_out, reg30_out;

  Register #(.width(32)) register_1 (.D({32{1'b0}}), .en(Register_0_on_off), .Q(reg0_out), .clk(Clock), .clr(Reset));
  Register #(.width(32)) register_2 (
    .D(Datos_de_entrada), .en(Register_1_on_off), .Q(reg1_out), .clk(Clock), .clr(Reset));
  Register #(.width(32)) register_3 (
    .D(Datos_de_entrada), .en(Register_2_on_off), .Q(reg2_out), .clk(Clock), .clr(Reset));
  Register #(.width(32)) register_4 (
    .D(Datos_de_entrada), .en(Register_3_on_off), .Q(reg3_out), .clk(Clock), .clr(Reset));
  Register #(.width(32)) register_5 (
    .D(Datos_de_entrada), .en(Register_4_on_off), .Q(reg4_out), .clk(Clock), .clr(Reset));
  Register #(.width(32)) register_6 (
    .D(Datos_de_entrada), .en(Register_5_on_off), .Q(reg5_out), .clk(Clock), .clr(Reset));
  Register #(.width(32)) register_7 (
    .D(Datos_de_entrada), .en(Register_6_on_off), .Q(reg6_out), .clk(Clock), .clr(Reset));
  Register #(.width(32)) register_8 (
    .D(Datos_de_entrada), .en(Register_7_on_off), .Q(reg7_out), .clk(Clock), .clr(Reset));
  Register #(.width(32)) register_9 (
    .D(Datos_de_entrada), .en(Register_8_on_off), .Q(reg8_out), .clk(Clock), .clr(Reset));
  Register #(.width(32)) register_10 (
    .D(Datos_de_entrada), .en(Register_9_on_off), .Q(reg9_out), .clk(Clock), .clr(Reset));
  Register #(.width(32)) register_11 (
    .D(Datos_de_entrada), .en(Register_10_on_off), .Q(reg10_out), .clk(Clock), .clr(Reset));
  Register #(.width(32)) register_12 (
    .D(Datos_de_entrada), .en(Register_11_on_off), .Q(reg11_out), .clk(Clock), .clr(Reset));
  Register #(.width(32)) register_13 (
    .D(Datos_de_entrada), .en(Register_12_on_off), .Q(reg12_out), .clk(Clock), .clr(Reset));
  Register #(.width(32)) register_14 (
    .D(Datos_de_entrada), .en(Register_13_on_off), .Q(reg13_out), .clk(Clock), .clr(Reset));
  Register #(.width(32)) register_15 (
    .D(Datos_de_entrada), .en(Register_14_on_off), .Q(reg14_out), .clk(Clock), .clr(Reset));
  Register #(.width(32)) register_16 (
    .D(Datos_de_entrada), .en(Register_15_on_off), .Q(reg15_out), .clk(Clock), .clr(Reset));
  Register #(.width(32)) register_17 (
    .D(Datos_de_entrada), .en(Register_16_on_off), .Q(reg16_out), .clk(Clock), .clr(Reset));
  Register #(.width(32)) register_18 (
    .D(Datos_de_entrada), .en(Register_17_on_off), .Q(reg17_out), .clk(Clock), .clr(Reset));
  Register #(.width(32)) register_19 (
    .D(Datos_de_entrada), .en(Register_16_on_off), .Q(reg18_out), .clk(Clock), .clr(Reset));
  Register #(.width(32)) register_20 (
    .D(Datos_de_entrada), .en(Register_17_on_off), .Q(reg19_out), .clk(Clock), .clr(Reset));
  Register #(.width(32)) register_21 (
    .D(Datos_de_entrada), .en(Register_20_on_off), .Q(reg20_out), .clk(Clock), .clr(Reset));
  Register #(.width(32)) register_22 (
    .D(Datos_de_entrada), .en(Register_21_on_off), .Q(reg21_out), .clk(Clock), .clr(Reset));
  Register #(.width(32)) register_23 (
    .D(Datos_de_entrada), .en(Register_22_on_off), .Q(reg22_out), .clk(Clock), .clr(Reset));
  Register #(.width(32)) register_24 (
    .D(Datos_de_entrada), .en(Register_23_on_off), .Q(reg23_out), .clk(Clock), .clr(Reset));
  Register #(.width(32)) register_25 (
    .D(Datos_de_entrada), .en(Register_24_on_off), .Q(reg24_out), .clk(Clock), .clr(Reset));
  Register #(.width(32)) register_26 (
    .D(Datos_de_entrada), .en(Register_25_on_off), .Q(reg25_out), .clk(Clock), .clr(Reset));
  Register #(.width(32)) register_27 (
    .D(Datos_de_entrada), .en(Register_26_on_off), .Q(reg26_out), .clk(Clock), .clr(Reset));
  Register #(.width(32)) register_28 (
    .D(Datos_de_entrada), .en(Register_27_on_off), .Q(reg27_out), .clk(Clock), .clr(Reset));
  Register #(.width(32)) register_29 (
    .D(Datos_de_entrada), .en(Register_28_on_off), .Q(reg28_out), .clk(Clock), .clr(Reset));
  Register #(.width(32)) register_30 (
    .D(Datos_de_entrada), .en(Register_29_on_off), .Q(reg29_out), .clk(Clock), .clr(Reset));
  Register #(.width(32)) register_31 (
    .D(Datos_de_entrada), .en(Register_30_on_off), .Q(reg30_out), .clk(Clock), .clr(Reset));
  Multiplexer #(.width(32), .enable("false")) multiplexer_1 (
    .in0(Datos_de_entrada), .in1(32'hffffc), .out(multiplexer_1_out), .sel(Reset));
  Register #(.width(32)) register_32 (.D(multiplexer_1_out), .en(or_1_out), .Q(SP), .clk(Clock));  // open: clr
  or or_1 (or_1_out, Reset, Register_31_on_off);
  Demultiplexer #(.select(5)) demultiplexer_1 (
    .out0(Register_0_on_off), .out1(Register_1_on_off), .out2(Register_2_on_off), .out3(Register_3_on_off),
    .out4(Register_4_on_off), .out5(Register_5_on_off), .out6(Register_6_on_off), .out7(Register_7_on_off),
    .out8(Register_8_on_off), .out9(Register_9_on_off), .out10(Register_10_on_off),
    .out11(Register_11_on_off), .out12(Register_12_on_off), .out13(Register_13_on_off),
    .out14(Register_14_on_off), .out15(Register_15_on_off), .out16(Register_16_on_off),
    .out17(Register_17_on_off), .out18(Register_18_on_off), .out19(Register_19_on_off),
    .out20(Register_20_on_off), .out21(Register_21_on_off), .out22(Register_22_on_off),
    .out23(Register_23_on_off), .out24(Register_24_on_off), .out25(Register_25_on_off),
    .out26(Register_26_on_off), .out27(Register_27_on_off), .out28(Register_28_on_off),
    .out29(Register_29_on_off), .out30(Register_30_on_off), .out31(Register_31_on_off), .in(Read_Write),
    .sel(\Dirección_de_destino ));  // open: en
  Multiplexer #(.select(5), .width(32), .enable("false")) multiplexer_2 (
    .in0(reg0_out), .in1(reg1_out), .in2(reg2_out), .in3(reg3_out), .in4(reg4_out), .in5(reg5_out),
    .in6(reg6_out), .in7(reg7_out), .in8(reg8_out), .in9(reg9_out), .in10(reg10_out), .in11(reg11_out),
    .in12(reg12_out), .in13(reg13_out), .in14(reg14_out), .in15(reg15_out), .in16(reg16_out),
    .in17(reg17_out), .in18(reg18_out), .in19(reg19_out), .in20(reg20_out), .in21(reg21_out),
    .in22(reg22_out), .in23(reg23_out), .in24(reg24_out), .in25(reg25_out), .in26(reg26_out),
    .in27(reg27_out), .in28(reg28_out), .in29(reg29_out), .in30(reg30_out), .in31(SP), .out(Read_Data_1),
    .sel(Selector_de_salida_A));
  Multiplexer #(.select(5), .width(32)) multiplexer_3 (
    .in0(reg0_out), .in1(reg1_out), .in2(reg2_out), .in3(reg3_out), .in4(reg4_out), .in5(reg5_out),
    .in6(reg6_out), .in7(reg7_out), .in8(reg8_out), .in9(reg9_out), .in10(reg10_out), .in11(reg11_out),
    .in12(reg12_out), .in13(reg13_out), .in14(reg14_out), .in15(reg15_out), .in16(reg16_out),
    .in17(reg17_out), .in18(reg18_out), .in19(reg19_out), .in20(reg20_out), .in21(reg21_out),
    .in22(reg22_out), .in23(reg23_out), .in24(reg24_out), .in25(reg25_out), .in26(reg26_out),
    .in27(reg27_out), .in28(reg28_out), .in29(reg29_out), .in30(reg30_out), .in31(SP), .out(Read_Data_2),
    .sel(Selector_de_salida_B));  // open: en

  // Other names for the same wires on the sheet: clk = Clock; input_value[31:0] = Datos_de_entrada; R_W = Read_Write;
  //   read_dataA[31:0] = Read_Data_1; read_dataB[31:0] = Read_Data_2; read_regA[4:0] = Selector_de_salida_A;
  //   read_regB[4:0] = Selector_de_salida_B; reg31_out[31:0] = SP; write_reg[4:0] = \Dirección_de_destino 

  // Notes on the sheet:
  //   Inputs
  //   OUTPUTS from your circuit
endmodule

module BranchControl (
  input  Zero,
  input  Less,
  input  Greater,
  input  Equals,
  input  [5:0] BranchFunction,
  output Condition
);

  wire not_1_out, or_1_out;

  or or_1 (or_1_out, Less, Equals);
  not not_1 (not_1_out, Zero);
  Multiplexer #(.select(3), .enable("false")) multiplexer_1 (
    .in1(Less), .in4(Zero), .in5(not_1_out), .in6(or_1_out), .in7(Greater), .out(Condition),
    .sel(BranchFunction[2:0]));  // open: in0, in2, in3
endmodule

module ControlUnit (
  input  MemReadEnd,
  input  MemWriteEnd,
  input  [5:0] OpCode,
  input  [5:0] FuncCode,
  input  Reset,
  input  Clock,
  output IorD,
  output [1:0] RegDst,
  output [1:0] RegWriteSelector,
  output [1:0] ALUSrcA,
  output [1:0] ALUSrcB,
  output Branch,
  output PCWrite,
  output RegWrite,
  output [1:0] PCSrc,
  output [5:0] ALUControl,
  output IRWrite,
  output MemWrite,
  output MemRead,
  output ExtOp,
  output HiLo_RW,
  output HiLo_Selector,
  output OutA,
  output STOP,
  output TTY_ENABLE,
  output KBD_ENABLE,
  output KBD_INPUT
);

  wire add_out, ALUControlIType, ALUControlRes, ALUControlRType, ALUControlSum, ALUControlSum_2,
       ALUControlSum_3, ALUControlSum_4, ALUSrcA_00, ALUSrcA_01, ALUSrcA_01_2, ALUSrcB_01, ALUSrcB_10,
       ALUToReg, ALUToReg_1, ALUToReg_2, ALUToReg_3, ALUToReg_4, and_4_out, and_15_out, and_out, andi_out,
       beq_out, bgtz_out, blez_out, bltz_out, bne_out, branch_inst, buffer_1_out, comparator_1_eq,
       comparator_2_eq, comparator_3_eq, comparator_4_eq, comparator_5_eq, comparator_6_eq, comparator_7_eq,
       comparator_8_eq, comparator_9_eq, comparator_10_eq, comparator_11_eq, comparator_12_eq,
       comparator_13_eq, comparator_14_eq, comparator_15_eq, comparator_16_eq, comparator_17_eq,
       comparator_18_eq, comparator_19_eq, comparator_20_eq, comparator_21_eq, comparator_22_eq,
       comparator_23_eq, comparator_24_eq, comparator_25_eq, comparator_26_eq, comparator_27_eq,
       comparator_28_eq, comparator_29_eq, comparator_30_eq, comparator_31_eq, comparator_32_eq,
       comparator_33_eq, comparator_34_eq, comparator_35_eq, comparator_36_eq, comparator_37_eq,
       comparator_38_eq, comparator_39_eq, Decode_2_q, demultiplexer_1_out0, demultiplexer_2_out0,
       demultiplexer_2_out1, demultiplexer_3_out0, demultiplexer_4_out0, demultiplexer_5_out0,
       demultiplexer_5_out1, demultiplexer_6_out0, demultiplexer_6_out1, div_out, divu_out, gotoIDLE, halt,
       HILOToReg, I_type, IDLE_q, IorD_0_1, IorD_2, IorD_3, IorD_4, IorD_5, j, jr, kbd, lw, MemToReg, mfhi,
       mflo, mult_out, multu_out, nop, nor_out, not_1_out, or_2_out, or_5_out, or_7_out, or_21_out,
       or_22_out, or_24_out, or_25_out, or_26_out, or_27_out, or_out, ori_out, PCSrc_10, PCSrc_11, pop, push,
       push_pop_out, R_Instruction, \rand , RandomToReg, RegDest_10, RegDst_0, RegDst_1, SelectHI, SelectLO,
       slt_out, slti_out, sltiu_out, sltu_out, special, sub_out, sw, tty, undriven, Write_to_PC_2_q, xor_out,
       xori_out;
  wire [1:0] priority_encoder_2_out;
  wire [2:0] priority_encoder_1_out;
  wire [5:0] I_Operation;

  buf u_special (special, comparator_1_eq);
  Comparator #(.width(6)) comparator_1 (.a(OpCode), .b({6{1'b1}}), .eq(comparator_1_eq));  // open: gt, lt
  buf u_sw (sw, comparator_2_eq);
  Comparator #(.width(6)) comparator_2 (.a(OpCode), .b(6'b101011), .eq(comparator_2_eq));  // open: gt, lt
  Comparator #(.width(6)) comparator_3 (.a(OpCode), .b(6'b100011), .eq(comparator_3_eq));  // open: gt, lt
  buf u_lw (lw, comparator_3_eq);
  buf xori (xori_out, comparator_4_eq);
  Comparator #(.width(6)) comparator_4 (.a(OpCode), .b(6'b001110), .eq(comparator_4_eq));  // open: gt, lt
  buf ori (ori_out, comparator_5_eq);
  Comparator #(.width(6)) comparator_5 (.a(OpCode), .b(6'b001101), .eq(comparator_5_eq));  // open: gt, lt
  buf andi (andi_out, comparator_6_eq);
  Comparator #(.width(6)) comparator_6 (.a(OpCode), .b(6'b001100), .eq(comparator_6_eq));  // open: gt, lt
  Comparator #(.width(6)) comparator_7 (.a(OpCode), .b(6'b001011), .eq(comparator_7_eq));  // open: gt, lt
  buf sltiu (sltiu_out, comparator_7_eq);
  buf slti (slti_out, comparator_8_eq);
  Comparator #(.width(6)) comparator_8 (.a(OpCode), .b(6'b001010), .eq(comparator_8_eq));  // open: gt, lt
  buf buffer_1 (buffer_1_out, comparator_9_eq);
  Comparator #(.width(6)) comparator_9 (.a(OpCode), .b(6'b001000), .eq(comparator_9_eq));  // open: gt, lt
  buf bgtz (bgtz_out, comparator_10_eq);
  Comparator #(.width(6)) comparator_10 (.a(OpCode), .b(6'b000111), .eq(comparator_10_eq));  // open: gt, lt
  buf blez (blez_out, comparator_11_eq);
  Comparator #(.width(6)) comparator_11 (.a(OpCode), .b(6'b000110), .eq(comparator_11_eq));  // open: gt, lt
  Comparator #(.width(6)) comparator_12 (.a(OpCode), .b(6'b000101), .eq(comparator_12_eq));  // open: gt, lt
  buf bne (bne_out, comparator_12_eq);
  Comparator #(.width(6)) comparator_13 (.a(OpCode), .b(6'b000100), .eq(comparator_13_eq));  // open: gt, lt
  buf beq (beq_out, comparator_13_eq);
  buf u_j (j, comparator_14_eq);
  Comparator #(.width(6)) comparator_14 (.a(OpCode), .b(6'b000010), .eq(comparator_14_eq));  // open: gt, lt
  Comparator #(.width(6)) comparator_15 (.a(OpCode), .b(6'b000001), .eq(comparator_15_eq));  // open: gt, lt
  buf bltz (bltz_out, comparator_15_eq);
  Comparator #(.width(6)) comparator_16 (.a(OpCode), .b({6{1'b0}}), .eq(comparator_16_eq));  // open: gt, lt
  Comparator #(.width(6)) comparator_17 (.a(OpCode), .b(6'b111000), .eq(comparator_17_eq));  // open: gt, lt
  buf push_pop (push_pop_out, comparator_17_eq);
  and add (add_out, comparator_16_eq, comparator_18_eq);
  Comparator #(.width(6)) comparator_18 (.a(FuncCode), .b(6'b100000), .eq(comparator_18_eq));  // open: gt, lt
  and sub (sub_out, comparator_16_eq, comparator_19_eq);
  Comparator #(.width(6)) comparator_19 (.a(FuncCode), .b(6'b100010), .eq(comparator_19_eq));  // open: gt, lt
  and mult (mult_out, comparator_16_eq, comparator_20_eq);
  Comparator #(.width(6)) comparator_20 (.a(FuncCode), .b(6'b011000), .eq(comparator_20_eq));  // open: gt, lt
  and multu (multu_out, comparator_16_eq, comparator_21_eq);
  Comparator #(.width(6)) comparator_21 (.a(FuncCode), .b(6'b011001), .eq(comparator_21_eq));  // open: gt, lt
  and div (div_out, comparator_16_eq, comparator_22_eq);
  Comparator #(.width(6)) comparator_22 (.a(FuncCode), .b(6'b011010), .eq(comparator_22_eq));  // open: gt, lt
  and divu (divu_out, comparator_16_eq, comparator_23_eq);
  Comparator #(.width(6)) comparator_23 (.a(FuncCode), .b(6'b011011), .eq(comparator_23_eq));  // open: gt, lt
  and \and  (and_out, comparator_16_eq, comparator_24_eq);
  Comparator #(.width(6)) comparator_24 (.a(FuncCode), .b(6'b100100), .eq(comparator_24_eq));  // open: gt, lt
  and \or  (or_out, comparator_16_eq, comparator_25_eq);
  Comparator #(.width(6)) comparator_25 (.a(FuncCode), .b(6'b100101), .eq(comparator_25_eq));  // open: gt, lt
  and \nor  (nor_out, comparator_16_eq, comparator_26_eq);
  Comparator #(.width(6)) comparator_26 (.a(FuncCode), .b(6'b100111), .eq(comparator_26_eq));  // open: gt, lt
  and \xor  (xor_out, comparator_16_eq, comparator_27_eq);
  Comparator #(.width(6)) comparator_27 (.a(FuncCode), .b(6'b101000), .eq(comparator_27_eq));  // open: gt, lt
  and slt (slt_out, comparator_16_eq, comparator_28_eq);
  Comparator #(.width(6)) comparator_28 (.a(FuncCode), .b(6'b101010), .eq(comparator_28_eq));  // open: gt, lt
  and sltu (sltu_out, comparator_16_eq, comparator_29_eq);
  Comparator #(.width(6)) comparator_29 (.a(FuncCode), .b(6'b101011), .eq(comparator_29_eq));  // open: gt, lt
  and u_mfhi (mfhi, comparator_16_eq, comparator_30_eq);
  Comparator #(.width(6)) comparator_30 (.a(FuncCode), .b(6'b010000), .eq(comparator_30_eq));  // open: gt, lt
  and u_mflo (mflo, comparator_16_eq, comparator_31_eq);
  Comparator #(.width(6)) comparator_31 (.a(FuncCode), .b(6'b010010), .eq(comparator_31_eq));  // open: gt, lt
  and u_nop (nop, comparator_16_eq, comparator_32_eq);
  Comparator #(.width(6)) comparator_32 (.a(FuncCode), .b({6{1'b0}}), .eq(comparator_32_eq));  // open: gt, lt
  and u_jr (jr, comparator_16_eq, comparator_33_eq);
  Comparator #(.width(6)) comparator_33 (.a(FuncCode), .b(6'b001000), .eq(comparator_33_eq));  // open: gt, lt
  and u_halt (halt, special, comparator_34_eq);
  Comparator #(.width(6)) comparator_34 (.a(FuncCode), .b({6{1'b1}}), .eq(comparator_34_eq));  // open: gt, lt
  and u_tty (tty, special, comparator_35_eq);
  Comparator #(.width(6)) comparator_35 (.a(FuncCode), .b(6'b000001), .eq(comparator_35_eq));  // open: gt, lt
  and u_rand (\rand , special, comparator_36_eq);
  Comparator #(.width(6)) comparator_36 (.a(FuncCode), .b(6'b000010), .eq(comparator_36_eq));  // open: gt, lt
  and u_kbd (kbd, special, comparator_37_eq);
  Comparator #(.width(6)) comparator_37 (.a(FuncCode), .b(6'b000100), .eq(comparator_37_eq));  // open: gt, lt
  Comparator #(.width(6)) comparator_38 (.a(FuncCode), .b({6{1'b0}}), .eq(comparator_38_eq));  // open: gt, lt
  Comparator #(.width(6)) comparator_39 (.a(FuncCode), .b(6'b000001), .eq(comparator_39_eq));  // open: gt, lt
  or or_2 (or_2_out, xori_out, ori_out, andi_out);
  or or_3 (branch_inst, bgtz_out, blez_out, bne_out, beq_out, bltz_out);
  and u_pop (pop, push_pop_out, comparator_38_eq);
  and u_push (push, push_pop_out, comparator_39_eq);
  D_Flip_Flop IDLE (.clk(Clock), .D(gotoIDLE), .Q(IDLE_q), .preset(Reset));  // open: Qn, en, reset
  and and_2 (ExtOp, ALUControlIType, or_2_out);
  or or_4 (I_type, xori_out, ori_out, andi_out, sltiu_out, slti_out, buffer_1_out);
  or or_5 (or_5_out, mult_out, multu_out, div_out, divu_out);
  or or_6 (R_Instruction, add_out, sub_out, mult_out, multu_out, div_out, divu_out, and_out, or_out, nor_out, xor_out, slt_out, sltu_out);
  and and_3 (HiLo_RW, or_5_out, ALUSrcA_01_2);
  or or_7 (or_7_out, demultiplexer_1_out0, IDLE_q);
  D_Flip_Flop LoadInst (.clk(Clock), .D(or_7_out), .Q(IorD_0_1), .reset(Reset));  // open: Qn, preset, en
  Priority_Encoder priority_encoder_1 (
    .in0(xori_out), .in1(ori_out), .in2(andi_out), .in3(sltiu_out), .in4(slti_out), .in5(buffer_1_out),
    .out(priority_encoder_1_out));  // open: in6, in7, en_in, gs, en_out
  Multiplexer #(.select(3), .width(6), .enable("false")) multiplexer_1 (
    .in0(6'b101000), .in1(6'b100101), .in2(6'b100100), .in3(6'b101011), .in4(6'b101010), .in5(6'b100000),
    .out(I_Operation), .sel(priority_encoder_1_out));  // open: in6, in7
  Demultiplexer #(.enable("false")) demultiplexer_1 (
    .out0(demultiplexer_1_out0), .out1(IRWrite), .in(IorD_0_1), .sel(MemReadEnd));
  Priority_Encoder #(.select(2)) priority_encoder_2 (
    .in0(ALUControlSum), .in1(ALUControlRes), .in2(ALUControlRType), .in3(ALUControlIType),
    .out(priority_encoder_2_out));  // open: gs, en_out, en_in
  or or_8 (ALUSrcA_00, IRWrite, ALUControlSum_2);
  or or_9 (ALUSrcB_10, ALUControlSum_3, ALUControlIType);
  // Probe on RegWriteSelector
  Priority_Encoder #(.select(2)) priority_encoder_3 (
    .in0(ALUToReg), .in1(MemToReg), .in2(HILOToReg), .in3(RandomToReg), .out(RegWriteSelector));  // open: gs, en_out, en_in
  Multiplexer #(.select(2), .width(6), .enable("false")) multiplexer_2 (
    .in0(6'b100000), .in1(6'b100010), .in2(FuncCode), .in3(I_Operation), .out(ALUControl),
    .sel(priority_encoder_2_out));
  Priority_Encoder #(.select(2)) priority_encoder_4 (
    .in0(ALUSrcA_01_2), .in1(ALUSrcB_01), .in2(ALUSrcB_10), .in3(ALUControlSum_2), .out(ALUSrcB));  // open: gs, en_out, en_in
  or or_10 (ALUSrcA_01, ALUControlSum_3, ALUSrcA_01_2, ALUSrcA_01_2, ALUControlIType);
  or or_11 (ALUSrcB_01, IRWrite, ALUControlSum_4, ALUControlSum_4);
  or or_12 (PCWrite, IRWrite, PCSrc_10, PCSrc_11);
  or or_13 (ALUToReg, ALUToReg_1, ALUToReg_2, ALUToReg_3, ALUToReg_4);
  or or_14 (RegWrite, MemToReg, ALUToReg_1, ALUToReg_2, HILOToReg, ALUToReg_3, ALUToReg_4, RandomToReg, MemToReg);
  // Probe on ALUControl
  // Probe on ALUSrcB
  not not_1 (not_1_out, IorD_0_1);
  or or_15 (MemWrite, IorD_2, IorD_4);
  D_Flip_Flop Decode (.clk(Clock), .D(IRWrite), .Q(ALUControlSum_2), .reset(Reset));  // open: Qn, preset, en
  Priority_Encoder #(.select(2)) priority_encoder_5 (
    .in0(IRWrite), .in1(Branch), .in2(PCSrc_10), .out(PCSrc));  // open: in3, gs, en_out, en_in
  // Probe on HiLo_Selector
  Priority_Encoder #(.select(1)) priority_encoder_6 (
    .in0(SelectLO), .in1(SelectHI), .out(HiLo_Selector));  // open: gs, en_out, en_in
  Priority_Encoder #(.select(2)) priority_encoder_7 (
    .in0(RegDst_0), .in1(RegDst_1), .in2(RegDest_10), .out(RegDst));  // open: in3, gs, en_out, en_in
  Priority_Encoder #(.select(2)) priority_encoder_8 (
    .in0(ALUSrcA_00), .in1(ALUSrcA_01), .in2(ALUControlSum_4), .in3(undriven), .out(ALUSrcA));  // open: gs, en_out, en_in
  or or_16 (IorD, not_1_out, IorD_2, IorD_3, IorD_4, IorD_5);
  or or_17 (MemRead, IorD_0_1, IorD_3, IorD_5);
  or or_18 (ALUControlSum, IRWrite, ALUControlSum_2, ALUControlSum_3, ALUControlSum_4);
  or or_19 (RegDst_0, MemToReg, ALUToReg_2, MemToReg);
  or or_20 (RegDst_1, ALUToReg_1, HILOToReg, ALUToReg_3, ALUToReg_4, MemToReg, RandomToReg);
  // Probe on PCSrc
  // Probe on RegDst
  // Probe on ALUSrcA
  D_Flip_Flop Decode_2 (.clk(Clock), .D(ALUControlSum_2), .Q(Decode_2_q), .reset(Reset));  // open: Qn, preset, en
  or or_21 (or_21_out, sw, lw);
  and and_4 (and_4_out, nop, Decode_2_q);
  and and_5 (ALUControlSum_3, or_21_out, Decode_2_q);
  and and_6 (ALUSrcA_01_2, R_Instruction, Decode_2_q);
  and and_7 (Branch, branch_inst, Decode_2_q);
  and and_8 (ALUControlIType, I_type, Decode_2_q);
  and and_9 (PCSrc_10, j, Decode_2_q);
  and and_10 (PCSrc_11, jr, Decode_2_q);
  and and_11 (SelectHI, mfhi, Decode_2_q);
  and and_12 (SelectLO, mflo, Decode_2_q);
  and and_13 (ALUControlSum_4, push, Decode_2_q);
  and and_14 (ALUControlSum_4, pop, Decode_2_q);
  and and_15 (and_15_out, halt, Decode_2_q);
  and and_16 (OutA, tty, Decode_2_q);
  and and_17 (RandomToReg, \rand , Decode_2_q);
  and and_18 (KBD_ENABLE, kbd, Decode_2_q);
  assign ALUControlRType = ALUSrcA_01_2 ? ALUSrcA_01_2 : 1'bz;  // Controlled_Buffer controlled_buffer_1
  assign ALUControlRes = ALUControlSum_4 ? ALUControlSum_4 : 1'bz;  // Controlled_Buffer controlled_buffer_2
  or or_22 (or_22_out, and_15_out, STOP);
  assign ALUControlRes = Branch ? Branch : 1'bz;  // Controlled_Buffer controlled_buffer_3
  or or_23 (HILOToReg, SelectHI, SelectLO);
  or or_24 (or_24_out, demultiplexer_3_out0, ALUControlSum_4);
  or or_25 (or_25_out, demultiplexer_4_out0, ALUControlSum_4);
  D_Flip_Flop u_STOP (.clk(Clock), .D(or_22_out), .Q(STOP), .reset(Reset));  // open: Qn, preset, en
  Demultiplexer #(.enable("false")) demultiplexer_2 (
    .out0(demultiplexer_2_out0), .out1(demultiplexer_2_out1), .in(ALUControlSum_3), .sel(lw));
  D_Flip_Flop R_Inst (.clk(Clock), .D(ALUSrcA_01_2), .Q(ALUToReg_1), .reset(Reset));  // open: Qn, preset, en
  D_Flip_Flop Write_to_PC (.clk(Clock), .D(ALUControlIType), .Q(ALUToReg_2), .reset(Reset));  // open: Qn, preset, en
  assign OutA = IorD_4 ? IorD_4 : 1'bz;  // Controlled_Buffer controlled_buffer_4
  D_Flip_Flop Write_to_Mem (.clk(Clock), .D(or_24_out), .Q(IorD_4), .reset(Reset));  // open: Qn, preset, en
  assign OutA = IorD_5 ? IorD_5 : 1'bz;  // Controlled_Buffer controlled_buffer_5
  D_Flip_Flop Load (.clk(Clock), .D(or_25_out), .Q(IorD_5), .reset(Reset));  // open: Qn, preset, en
  D_Flip_Flop Read_kbd (.clk(Clock), .D(KBD_ENABLE), .Q(KBD_INPUT), .reset(Reset));  // open: Qn, preset, en
  or or_26 (or_26_out, demultiplexer_5_out0, demultiplexer_2_out0);
  or or_27 (or_27_out, demultiplexer_6_out0, demultiplexer_2_out1);
  Demultiplexer #(.enable("false")) demultiplexer_3 (
    .out0(demultiplexer_3_out0), .out1(ALUToReg_3), .in(IorD_4), .sel(MemWriteEnd));
  Demultiplexer #(.enable("false")) demultiplexer_4 (
    .out0(demultiplexer_4_out0), .out1(ALUToReg_4), .in(IorD_5), .sel(MemReadEnd));
  D_Flip_Flop sw_2 (.clk(Clock), .D(or_26_out), .Q(IorD_2), .reset(Reset));  // open: Qn, preset, en
  D_Flip_Flop lw_2 (.clk(Clock), .D(or_27_out), .Q(IorD_3), .reset(Reset));  // open: Qn, preset, en
  D_Flip_Flop Write_to_PC_2 (.clk(Clock), .D(Branch), .Q(Write_to_PC_2_q), .reset(Reset));  // open: Qn, preset, en
  D_Flip_Flop WriteToReg (.clk(Clock), .D(KBD_INPUT), .Q(MemToReg), .reset(Reset));  // open: Qn, preset, en
  Demultiplexer #(.enable("false")) demultiplexer_5 (
    .out0(demultiplexer_5_out0), .out1(demultiplexer_5_out1), .in(IorD_2), .sel(MemWriteEnd));
  Demultiplexer #(.enable("false")) demultiplexer_6 (
    .out0(demultiplexer_6_out0), .out1(demultiplexer_6_out1), .in(IorD_3), .sel(MemReadEnd));
  D_Flip_Flop Write_to_Reg (
    .clk(Clock), .D(demultiplexer_6_out1), .Q(MemToReg), .reset(Reset));  // open: Qn, preset, en
  D_Flip_Flop WriteToReg_2 (.clk(Clock), .D(ALUToReg_4), .Q(MemToReg), .reset(Reset));  // open: Qn, preset, en
  assign RegWrite = MemToReg ? MemToReg : 1'bz;  // Controlled_Buffer controlled_buffer_6
  or or_28 (gotoIDLE, and_4_out, demultiplexer_5_out1, MemToReg, ALUToReg_1, Write_to_PC_2_q, ALUToReg_2, PCSrc_10, PCSrc_11, HILOToReg, ALUToReg_3, MemToReg, OutA, RandomToReg, MemToReg);

  assign TTY_ENABLE = OutA;

  // Other names for the same wires on the sheet: ALUSrcA_10 = ALUControlSum_4; ALUSrcB_01_2 = ALUControlSum_4;
  //   ALUSrcB_01_3 = ALUControlSum_4; ALUSrcA_01_1 = ALUControlSum_3; ALUSrcB_10_1 = ALUControlSum_3;
  //   ALUSrcA_00_2 = ALUControlSum_2; ALUSrcB_11 = ALUControlSum_2; CLK = Clock; CLR = Reset;
  //   ALUSrcA_01_4 = ALUControlIType; ALUSrcB_10_2 = ALUControlIType; extF = ALUControlIType; MemRead_1 = IorD_0_1;
  //   MemRead_2 = IorD_3; MemRead_3 = IorD_5; MemWrite_1 = IorD_2; MemWrite_2 = IorD_4; PCSrc_01 = Branch;
  //   ALUControlSum_1 = IRWrite; ALUSrcA_00_1 = IRWrite; ALUSrcB_01_1 = IRWrite; PCSrc_00 = IRWrite;
  //   PCWrite_1 = IRWrite; PCWrite_2 = PCSrc_10; PCWrite_3 = PCSrc_11; RegDst_1_1 = ALUToReg_1;
  //   RegWrite_2 = ALUToReg_1; RegDst_0_2 = ALUToReg_2; RegWrite_3 = ALUToReg_2; RegDst_1_2 = HILOToReg;
  //   RegWrite_4 = HILOToReg; RegDst_1_3 = ALUToReg_3; RegWrite_5 = ALUToReg_3; RegDst_1_4 = ALUToReg_4;
  //   RegWrite_6 = ALUToReg_4; RegDst_1_6 = RandomToReg; RegWrite_7 = RandomToReg; RegDst_0_1 = MemToReg;
  //   RegDst_0_3 = MemToReg; RegDst_1_5 = MemToReg; RegWrite_1 = MemToReg; RegWrite_8 = MemToReg;
  //   ALUSrcA_01_3 = ALUSrcA_01_2; ALUSrcB_00 = ALUSrcA_01_2; WriteHiLo = ALUSrcA_01_2

  // Notes on the sheet:
  //   INPUTS
  //   addi
  //   OUTPUTS
  //   Load PC Address
  //   Write Inst
  //   FETCH INSTRUCTION
  //   ALU Control
  //   ALU PC+4
  //   ALU (PC+4)x4
endmodule

module Extender (
  input  [15:0] Input,
  input  ExtOp,
  output [31:0] out_3
);

  wire [31:0] bit_extender_1_out, bit_extender_2_out;

  assign bit_extender_1_out = {{16{Input[15]}}, Input};  // Bit_Extender bit_extender_1
  assign bit_extender_2_out = {{16{1'b0}}, Input};  // Bit_Extender bit_extender_2
  Multiplexer #(.width(32), .enable("false")) multiplexer_1 (
    .in0(bit_extender_1_out), .in1(bit_extender_2_out), .out(out_3), .sel(ExtOp));
endmodule

module ALU (
  input  [31:0] Op1,
  input  [31:0] Op2,
  input  [5:0] Instruction,
  output [31:0] HI,
  output [31:0] LO,
  output [31:0] Output,
  output Carry,
  output Zero,
  output Overflow,
  output Greater,
  output Equals,
  output Less
);

  wire adder_1_cout, and_1_out, and_2_out, and_3_out, and_4_out, and_5_out, and_6_out, comparator_2_lt,
       comparator_3_lt, comparator_5_eq, comparator_6_eq, is_div, is_divu, is_mult, is_multu, not_1_out,
       subtractor_1_bout, xor_1_out, xor_2_out, xor_3_out, xor_4_out;
  wire [31:0] \and , div_hi, div_lo, divu_hi, divu_lo, mult_hi, mult_lo, multu_hi, multu_lo, \nor , \or ,
       slt, sltu, sub, sum, \xor ;

  Decoder #(.select(5), .disabled(0)) decoder_1 (
    .out24(is_mult), .out25(is_multu), .out26(is_divu), .out27(is_div), .sel(Instruction[4:0]), .en(not_1_out));  // open: out0, out1, out2, out3, out4, out5, out6, out7, out8, out9, out10, out11, out12, out13, out14, out15, out16, out17, out18, out19, out20, out21, out22, out23, out28, out29, out30, out31
  not not_1 (not_1_out, Instruction[5]);
  // Probe on Op1
  // Probe on Op2
  Comparator #(.width(32)) comparator_1 (.a(Op1), .b({32{1'b0}}), .gt(Greater), .eq(Equals), .lt(Less));
  Comparator #(.width(32)) comparator_2 (.a(Op1), .b(Op2), .lt(comparator_2_lt));  // open: gt, eq
  Adder #(.width(32)) adder_1 (.a(Op1), .b(Op2), .out(sum), .cin(1'b0), .cout(adder_1_cout));
  Subtractor #(.width(32)) subtractor_1 (.a(Op1), .b(Op2), .out(sub), .bin(1'b0), .bout(subtractor_1_bout));
  Multiplexer #(.width(32), .enable("false")) multiplexer_1 (
    .in0({32{1'b0}}), .in1(32'h1), .out(slt), .sel(comparator_2_lt));
  xor xor_1 (xor_1_out, Op1[31], sum[31]);
  xor xor_2 (xor_2_out, sum[31], Op2[31]);
  xor xor_3 (xor_3_out, Op1[31], sub[31]);
  xor xor_4 (xor_4_out, sub[31], Op2[31]);
  Multiplexer #(.select(5), .width(32)) multiplexer_2 (
    .in0(sum), .in2(sub), .in4(\and ), .in5(\or ), .in7(\nor ), .in8(\xor ), .in10(slt), .in11(sltu),
    .out(Output), .sel(Instruction[4:0]), .en(Instruction[5]));  // open: in1, in3, in6, in9, in12, in13, in14, in15, in16, in17, in18, in19, in20, in21, in22, in23, in24, in25, in26, in27, in28, in29, in30, in31
  and and_1 (and_1_out, xor_1_out, xor_2_out);
  and and_2 (and_2_out, xor_3_out, xor_4_out);
  Comparator #(.width(32), .mode("unsigned")) comparator_3 (.a(Op1), .b(Op2), .lt(comparator_3_lt));  // open: gt, eq
  assign HI = is_div ? div_hi : 32'bz;  // Controlled_Buffer controlled_buffer_1
  assign LO = is_div ? div_lo : 32'bz;  // Controlled_Buffer controlled_buffer_2
  Comparator #(.width(32)) comparator_4 (.a(Output), .b({32{1'b0}}), .eq(Zero));  // open: gt, lt
  Comparator #(.width(6)) comparator_5 (.a(Instruction), .b(6'b100000), .eq(comparator_5_eq));  // open: gt, lt
  Comparator #(.width(6)) comparator_6 (.a(Instruction), .b(6'b100010), .eq(comparator_6_eq));  // open: gt, lt
  Multiplexer #(.width(32), .enable("false")) multiplexer_3 (
    .in0({32{1'b0}}), .in1(32'h1), .out(sltu), .sel(comparator_3_lt));
  assign HI = is_multu ? multu_hi : 32'bz;  // Controlled_Buffer controlled_buffer_3
  assign HI = is_mult ? mult_hi : 32'bz;  // Controlled_Buffer controlled_buffer_4
  assign HI = is_divu ? divu_hi : 32'bz;  // Controlled_Buffer controlled_buffer_5
  assign LO = is_multu ? multu_lo : 32'bz;  // Controlled_Buffer controlled_buffer_6
  assign LO = is_mult ? mult_lo : 32'bz;  // Controlled_Buffer controlled_buffer_7
  assign LO = is_divu ? divu_lo : 32'bz;  // Controlled_Buffer controlled_buffer_8
  and and_3 (and_3_out, and_1_out, comparator_5_eq);
  and and_4 (and_4_out, comparator_5_eq, adder_1_cout);
  or or_1 (Carry, and_4_out, and_5_out);
  and and_5 (and_5_out, subtractor_1_bout, comparator_6_eq);
  and and_6 (and_6_out, comparator_6_eq, and_2_out);
  or or_2 (Overflow, and_3_out, and_6_out);
  assign \and  = Op1 & Op2;  // AND_Gate and_7, 32 bits wide
  assign \or  = Op1 | Op2;  // OR_Gate or_3, 32 bits wide
  assign \nor  = ~(Op1 | Op2);  // NOR_Gate nor_1, 32 bits wide
  assign \xor  = Op1 ^ Op2;  // XOR_Gate xor_5, 32 bits wide
  Multiplier #(.width(32)) multiplier_1 (.a(Op1), .b(Op2), .out(mult_lo), .cout(mult_hi));  // open: cin
  Divider #(.width(32)) divider_1 (.a(Op1), .b(Op2), .out(divu_lo), .rem(divu_hi));  // open: upper
  UnsignedMultiplier unsignedmultiplier_1 (.A(Op1), .B(Op2), .Low(multu_lo), .Hi(multu_hi));
  SignDivider signdivider_1 (.A(Op1), .B(Op2), .Lo(div_lo), .Hi(div_hi));

  // Other names for the same wires on the sheet: opA[31:0] = Op1; opB[31:0] = Op2; Overflow_flag = Overflow;
  //   S[5:0] = Instruction

  // Notes on the sheet:
  //   INPUTS
  //   Outputs
  //   Flags
endmodule

module UnsignedMultiplier (
  input  [31:0] A,
  input  [31:0] B,
  output [31:0] Low,
  output [31:0] Hi
);

  wire [31:0] umultaux_1_output, umultaux_2_output, umultaux_3_output, umultaux_4_output, umultaux_5_output,
       umultaux_6_output, umultaux_7_output, umultaux_8_output, umultaux_9_output, umultaux_10_output,
       umultaux_11_output, umultaux_12_output, umultaux_13_output, umultaux_14_output, umultaux_15_output,
       umultaux_16_output, umultaux_17_output, umultaux_18_output, umultaux_19_output, umultaux_20_output,
       umultaux_21_output, umultaux_22_output, umultaux_23_output, umultaux_24_output, umultaux_25_output,
       umultaux_26_output, umultaux_27_output, umultaux_28_output, umultaux_29_output, umultaux_30_output,
       umultaux_31_output;

  // Probe on B
  // Probe on B
  // Probe on A
  // Probe on A
  UMultAux umultaux_1 (.A(A), .in_2(B[0]), .Last(Low[0]), .Prev({32{1'b0}}), .Output(umultaux_1_output));
  UMultAux umultaux_2 (.A(A), .in_2(B[1]), .Last(Low[1]), .Prev(umultaux_1_output), .Output(umultaux_2_output));
  UMultAux umultaux_3 (.A(A), .in_2(B[2]), .Last(Low[2]), .Prev(umultaux_2_output), .Output(umultaux_3_output));
  UMultAux umultaux_4 (.A(A), .in_2(B[3]), .Last(Low[3]), .Prev(umultaux_3_output), .Output(umultaux_4_output));
  UMultAux umultaux_5 (.A(A), .in_2(B[4]), .Last(Low[4]), .Prev(umultaux_4_output), .Output(umultaux_5_output));
  UMultAux umultaux_6 (.A(A), .in_2(B[5]), .Last(Low[5]), .Prev(umultaux_5_output), .Output(umultaux_6_output));
  UMultAux umultaux_7 (.A(A), .in_2(B[6]), .Last(Low[6]), .Prev(umultaux_6_output), .Output(umultaux_7_output));
  UMultAux umultaux_8 (.A(A), .in_2(B[7]), .Last(Low[7]), .Prev(umultaux_7_output), .Output(umultaux_8_output));
  UMultAux umultaux_9 (.A(A), .in_2(B[8]), .Last(Low[8]), .Prev(umultaux_8_output), .Output(umultaux_9_output));
  UMultAux umultaux_10 (.A(A), .in_2(B[9]), .Last(Low[9]), .Prev(umultaux_9_output), .Output(umultaux_10_output));
  UMultAux umultaux_11 (.A(A), .in_2(B[10]), .Last(Low[10]), .Prev(umultaux_10_output), .Output(umultaux_11_output));
  UMultAux umultaux_12 (.A(A), .in_2(B[11]), .Last(Low[11]), .Prev(umultaux_11_output), .Output(umultaux_12_output));
  UMultAux umultaux_13 (.A(A), .in_2(B[12]), .Last(Low[12]), .Prev(umultaux_12_output), .Output(umultaux_13_output));
  UMultAux umultaux_14 (.A(A), .in_2(B[13]), .Last(Low[13]), .Prev(umultaux_13_output), .Output(umultaux_14_output));
  UMultAux umultaux_15 (.A(A), .in_2(B[14]), .Last(Low[14]), .Prev(umultaux_14_output), .Output(umultaux_15_output));
  UMultAux umultaux_16 (.A(A), .in_2(B[15]), .Last(Low[15]), .Prev(umultaux_15_output), .Output(umultaux_16_output));
  UMultAux umultaux_17 (.A(A), .in_2(B[16]), .Last(Low[16]), .Prev(umultaux_16_output), .Output(umultaux_17_output));
  UMultAux umultaux_18 (.A(A), .in_2(B[17]), .Last(Low[17]), .Prev(umultaux_17_output), .Output(umultaux_18_output));
  UMultAux umultaux_19 (.A(A), .in_2(B[18]), .Last(Low[18]), .Prev(umultaux_18_output), .Output(umultaux_19_output));
  UMultAux umultaux_20 (.A(A), .in_2(B[19]), .Last(Low[19]), .Prev(umultaux_19_output), .Output(umultaux_20_output));
  UMultAux umultaux_21 (.A(A), .in_2(B[20]), .Last(Low[20]), .Prev(umultaux_20_output), .Output(umultaux_21_output));
  UMultAux umultaux_22 (.A(A), .in_2(B[21]), .Last(Low[21]), .Prev(umultaux_21_output), .Output(umultaux_22_output));
  UMultAux umultaux_23 (.A(A), .in_2(B[22]), .Last(Low[22]), .Prev(umultaux_22_output), .Output(umultaux_23_output));
  UMultAux umultaux_24 (.A(A), .in_2(B[23]), .Last(Low[23]), .Prev(umultaux_23_output), .Output(umultaux_24_output));
  UMultAux umultaux_25 (.A(A), .in_2(B[24]), .Last(Low[24]), .Prev(umultaux_24_output), .Output(umultaux_25_output));
  UMultAux umultaux_26 (.A(A), .in_2(B[25]), .Last(Low[25]), .Prev(umultaux_25_output), .Output(umultaux_26_output));
  UMultAux umultaux_27 (.A(A), .in_2(B[26]), .Last(Low[26]), .Prev(umultaux_26_output), .Output(umultaux_27_output));
  UMultAux umultaux_28 (.A(A), .in_2(B[27]), .Last(Low[27]), .Prev(umultaux_27_output), .Output(umultaux_28_output));
  UMultAux umultaux_29 (.A(A), .in_2(B[28]), .Last(Low[28]), .Prev(umultaux_28_output), .Output(umultaux_29_output));
  UMultAux umultaux_30 (.A(A), .in_2(B[29]), .Last(Low[29]), .Prev(umultaux_29_output), .Output(umultaux_30_output));
  UMultAux umultaux_31 (.A(A), .in_2(B[30]), .Last(Low[30]), .Prev(umultaux_30_output), .Output(umultaux_31_output));
  UMultAux umultaux_32 (.A(A), .in_2(B[31]), .Last(Low[31]), .Prev(umultaux_31_output), .Output(Hi));
  // Probe on Low
  // Probe on Low
  // Probe on Hi
  // Probe on Hi
endmodule

module UMultAux (
  input  [31:0] A,
  input  in_2,
  input  [31:0] Prev,
  output Last,
  output [31:0] Output
);

  wire [31:0] and_32_out;

  and and_1 (and_32_out[31], in_2, A[31]);
  and and_2 (and_32_out[30], in_2, A[30]);
  and and_3 (and_32_out[27], in_2, A[27]);
  and and_4 (and_32_out[28], in_2, A[28]);
  and and_5 (and_32_out[29], in_2, A[29]);
  and and_6 (and_32_out[26], in_2, A[26]);
  and and_7 (and_32_out[25], in_2, A[25]);
  and and_8 (and_32_out[23], in_2, A[23]);
  and and_9 (and_32_out[24], in_2, A[24]);
  and and_10 (and_32_out[22], in_2, A[22]);
  and and_11 (and_32_out[21], in_2, A[21]);
  and and_12 (and_32_out[20], in_2, A[20]);
  and and_13 (and_32_out[19], in_2, A[19]);
  and and_14 (and_32_out[17], in_2, A[17]);
  and and_15 (and_32_out[18], in_2, A[18]);
  and and_16 (and_32_out[15], in_2, A[15]);
  and and_17 (and_32_out[16], in_2, A[16]);
  and and_18 (and_32_out[14], in_2, A[14]);
  and and_19 (and_32_out[13], in_2, A[13]);
  and and_20 (and_32_out[11], in_2, A[11]);
  and and_21 (and_32_out[12], in_2, A[12]);
  Adder #(.width(32)) adder_1 (.a(and_32_out), .b(Prev), .out({Output[30:0], Last}));  // open: cin, cout
  and and_22 (and_32_out[10], in_2, A[10]);
  and and_23 (and_32_out[9], in_2, A[9]);
  and and_24 (and_32_out[6], in_2, A[6]);
  and and_25 (and_32_out[8], in_2, A[8]);
  and and_26 (and_32_out[7], in_2, A[7]);
  and and_27 (and_32_out[5], in_2, A[5]);
  and and_28 (and_32_out[3], in_2, A[3]);
  and and_29 (and_32_out[4], in_2, A[4]);
  and and_30 (and_32_out[1], in_2, A[1]);
  and and_31 (and_32_out[2], in_2, A[2]);
  and and_32 (and_32_out[0], in_2, A[0]);

  assign Output[31] = 1'b0;
endmodule

module SignDivider (
  input  [31:0] A,
  input  [31:0] B,
  output [31:0] Lo,
  output [31:0] Hi
);

  wire dif_sign;
  wire [31:0] divider_1_out, multiplexer_1_out, multiplexer_2_out, multiplier_1_out, multiplier_2_out,
       multiplier_3_out;

  // Probe on A
  // Probe on B
  Multiplier #(.width(32)) multiplier_1 (.a(A), .b({32{1'b1}}), .out(multiplier_1_out));  // open: cin, cout
  Multiplier #(.width(32)) multiplier_2 (.a({32{1'b1}}), .b(B), .out(multiplier_2_out));  // open: cin, cout
  Multiplexer #(.width(32), .enable("false")) multiplexer_1 (
    .in0(A), .in1(multiplier_1_out), .out(multiplexer_1_out), .sel(A[31]));
  xor xor_1 (dif_sign, A[31], B[31]);
  Multiplexer #(.width(32), .enable("false")) multiplexer_2 (
    .in0(B), .in1(multiplier_2_out), .out(multiplexer_2_out), .sel(B[31]));
  // Probe on multiplexer_1_out
  // Probe on multiplexer_2_out
  // Probe on divider_1_out
  Divider #(.width(32)) divider_1 (
    .a(multiplexer_1_out), .b(multiplexer_2_out), .out(divider_1_out), .rem(Hi));  // open: upper
  Multiplier #(.width(32)) multiplier_3 (.a(divider_1_out), .b({32{1'b1}}), .out(multiplier_3_out));  // open: cin, cout
  Multiplexer #(.width(32), .enable("false")) multiplexer_3 (
    .in0(divider_1_out), .in1(multiplier_3_out), .out(Lo), .sel(dif_sign));
  // Probe on Lo
  // Probe on Hi
endmodule

module InstructionRegister (
  input  [31:0] Instruction,
  input  Enable,
  input  CLK,
  input  Clear,
  output [5:0] Funct_code,
  output [4:0] X,
  output [4:0] Rd,
  output [4:0] Rt,
  output [4:0] Rs,
  output [5:0] Op_code,
  output [15:0] shamnt,
  output [31:0] Instruction_2
);

  Register #(.width(32)) u_Instruction (
    .D(Instruction), .en(Enable), .Q({Instruction_2[31:6], Funct_code}), .clk(CLK), .clr(Clear));

  assign Instruction_2[5:0] = Funct_code;
  assign Op_code = Instruction_2[31:26];
  assign Rd = Instruction_2[15:11];
  assign Rs = Instruction_2[25:21];
  assign Rt = Instruction_2[20:16];
  assign shamnt = {Instruction_2[15:6], Funct_code};
  assign X = Instruction_2[10:6];
endmodule

module Wait (
  input  Load,
  input  [3:0] Input,
  input  count,
  input  Clk,
  output Finished
);

  wire [3:0] counter_1_q;

  Counter #(.width(4), .max('hf)) counter_1 (
    .load(Load), .D(Input), .count(count), .Q(counter_1_q), .clk(Clk));  // open: carry, clr
  Comparator #(.width(4)) comparator_1 (.a(4'b0000), .b(counter_1_q), .eq(Finished));  // open: gt, lt
endmodule

module Cache (
  input  clk,
  input  [3:0] mask,
  input  [3:0] read,
  input  rst,
  input  [3:0] write,
  input  [15:0] address,
  input  r_w,
  input  cs,
  input  [31:0] ram_output0,
  input  [31:0] cpu_input0,
  input  [31:0] ram_output1,
  input  [31:0] cpu_input1,
  input  [31:0] ram_output2,
  input  [31:0] cpu_input_2,
  input  [31:0] ram_output3,
  input  [31:0] cpu_input3,
  output finish,
  output [3:0] ramMask,
  output [15:0] Ram_address,
  output rsmCS,
  output ramR_W,
  output [31:0] ram_input0,
  output [31:0] cpu_output0,
  output [31:0] ram_input1,
  output [31:0] cpu_output1,
  output [31:0] ram_input2,
  output [31:0] cpu_output2,
  output [31:0] ram_input3,
  output [31:0] cpu_output3
);

  wire and_9_out, and_10_out, and_11_out, and_12_out, and_15_out, and_16_out, and_17_out, and_18_out,
       and_19_out, and_20_out, and_21_out, and_22_out, clean, clean_0, clean_1, clean_3, clean_4, Cond,
       controlled_buffer_9_out, controlled_buffer_10_out, controlled_buffer_11_out, controlled_buffer_12_out,
       controlled_buffer_13_out, controlled_buffer_14_out, controlled_buffer_15_out,
       controlled_buffer_16_out, d_ff_1_q, d_ff_2_q, d_ff_3_q, d_ff_4_q, d_ff_5_q, d_ff_6_q, d_ff_7_q,
       d_ff_8_q, d_ff_9_q, dec, dec0, dec1, dec2, dec3, dec4, dec5, dec6, demultiplexer_1_out0,
       demultiplexer_1_out1, demultiplexer_2_out0, demultiplexer_2_out1, demultiplexer_3_out0,
       demultiplexer_3_out1, demultiplexer_4_out0, demultiplexer_4_out1, demultiplexer_5_out0,
       demultiplexer_5_out1, demultiplexer_6_out0, demultiplexer_6_out1, demultiplexer_7_out0,
       demultiplexer_7_out1, demultiplexer_8_out1, demultiplexer_9_out0, demultiplexer_9_out1,
       demultiplexer_13_out0, E0, E1, E2, E3, E4, E5, E6, E7, end2, end3, end5, end7, end8, enTag, enTag_0,
       enTag_1, enTag_2, enTag_3, enTag_4, finish_t, hit, load0, load1, load2, load3, loadW, loadW0, loadW1,
       loadW2, loadW3, loadW4, loadW5, loadW6, not_1_out, not_2_out, not_3_out, not_4_out, not_5_out,
       not_6_out, not_7_out, not_8_out, ON, On0, On1, On2, On3, On4, On5, On6, On7, or_10_out, or_11_out,
       or_12_out, or_13_out, or_21_out, or_22_out, out, R_W_INPUT, R_W_INPUT2, R_W_OUPUT, RAM_imput_S,
       ramCS1, ramCS2, ramCS3, ramCS4, ramCS5, ramCS6, Sel, Stime, v0, v1, v2, v3, v4, v5, v6, v7, valid, w0,
       w1, w2, w3, Write_sel;
  wire [3:0] multiplexer_1_out;
  wire [12:0] storedTAG, xnor_1_out;
  wire [31:0] controlled_buffer_1_out, controlled_buffer_3_out, controlled_buffer_5_out,
       controlled_buffer_7_out, ram_2_data, ram_3_data, ram_4_data, ram_5_data;

  Decoder #(.select(3), .enable("false")) decoder_1 (
    .out0(v0), .out1(v1), .out2(v2), .out3(v3), .out4(v4), .out5(v5), .out6(v6), .out7(v7), .sel(address[2:0]));
  Multiplexer #(.width(4), .enable("false")) multiplexer_1 (
    .in0(read), .in1(write), .out(multiplexer_1_out), .sel(Stime));
  or or_1 (Stime, loadW0, loadW3);
  or or_2 (ramR_W, RAM_imput_S, ramCS3);
  Multiplexer #(.width(32), .enable("false")) multiplexer_2 (
    .in0(cpu_input0), .in1(cpu_output0), .out(ram_input0), .sel(RAM_imput_S));
  Multiplexer #(.width(32), .enable("false")) multiplexer_3 (
    .in0(cpu_input1), .in1(cpu_output1), .out(ram_input1), .sel(RAM_imput_S));
  Multiplexer #(.width(32), .enable("false")) multiplexer_4 (
    .in0(cpu_input_2), .in1(cpu_output2), .out(ram_input2), .sel(RAM_imput_S));
  Multiplexer #(.width(32), .enable("false")) multiplexer_5 (
    .in0(cpu_input3), .in1(cpu_output3), .out(ram_input3), .sel(RAM_imput_S));
  Multiplexer #(.width(16), .enable("false")) multiplexer_6 (
    .in0(address), .in1({storedTAG, address[2:0]}), .out(Ram_address), .sel(RAM_imput_S));
  Wait wait_1 (.Input(multiplexer_1_out), .Finished(finish_t), .Load(loadW), .count(dec), .Clk(clk));
  or or_3 (rsmCS, RAM_imput_S, ramCS1, ramCS2, ramCS6, ramCS3, ramCS4, ramCS5);
  Multiplexer #(.width(4), .enable("false")) multiplexer_7 (
    .in0(mask), .in1(4'b1111), .out(ramMask), .sel(RAM_imput_S));
  and and_1 (E0, cs, v0);
  and and_2 (E1, cs, v1);
  and and_3 (E2, cs, v2);
  and and_4 (E3, cs, v3);
  or or_4 (load0, enTag_1, enTag_0, enTag_4, enTag_2, enTag_3);
  or or_5 (load1, enTag_0, enTag_1, enTag_4, enTag_2, enTag_3);
  or or_6 (load2, enTag_0, enTag_1, enTag_4, enTag_2, enTag_3);
  or or_7 (load3, enTag_0, enTag_1, enTag_4, enTag_2, enTag_3);
  and and_5 (E4, cs, v4);
  and and_6 (E5, cs, v5);
  and and_7 (E6, cs, v6);
  and and_8 (E7, cs, v7);
  and and_9 (and_9_out, mask[0], R_W_INPUT);
  and and_10 (and_10_out, mask[1], R_W_INPUT);
  and and_11 (and_11_out, mask[2], R_W_INPUT);
  and and_12 (and_12_out, mask[3], R_W_INPUT);
  or or_8 (loadW, loadW0, loadW1, loadW2, loadW6, loadW3, loadW4, loadW5);
  or or_9 (dec, dec0, dec1, dec2, dec6, dec3, dec4, dec5);
  // Probe on address
  assign controlled_buffer_1_out = and_9_out ? cpu_input0 : 32'bz;  // Controlled_Buffer controlled_buffer_1
  assign controlled_buffer_1_out = R_W_OUPUT ? ram_output0 : 32'bz;  // Controlled_Buffer controlled_buffer_2
  assign controlled_buffer_3_out = and_10_out ? cpu_input1 : 32'bz;  // Controlled_Buffer controlled_buffer_3
  assign controlled_buffer_3_out = R_W_OUPUT ? ram_output1 : 32'bz;  // Controlled_Buffer controlled_buffer_4
  assign controlled_buffer_5_out = and_11_out ? cpu_input_2 : 32'bz;  // Controlled_Buffer controlled_buffer_5
  assign controlled_buffer_5_out = R_W_OUPUT ? ram_output2 : 32'bz;  // Controlled_Buffer controlled_buffer_6
  assign controlled_buffer_7_out = and_12_out ? cpu_input3 : 32'bz;  // Controlled_Buffer controlled_buffer_7
  assign controlled_buffer_7_out = R_W_OUPUT ? ram_output3 : 32'bz;  // Controlled_Buffer controlled_buffer_8
  or or_10 (or_10_out, w0, load0);
  or or_11 (or_11_out, w1, load1);
  or or_12 (or_12_out, w2, load2);
  or or_13 (or_13_out, w3, load3);
  RAM_part #(.addrWidth(3), .dataWidth(13), .bus("separate")) ram_1 (
    .addr(address[2:0]), .din(address[15:3]), .data(storedTAG), .str(enTag), .sel(1'b1), .clk(clk),
    .ld(1'b1), .clr(rst));
  // Probe on address[2:0]
  RAM_part #(.addrWidth(3), .dataWidth(32), .bus("separate")) ram_2 (
    .addr(address[2:0]), .din(controlled_buffer_1_out), .data(ram_2_data), .str(or_10_out), .sel(cs),
    .clk(clk), .ld(out), .clr(rst));
  RAM_part #(.addrWidth(3), .dataWidth(32), .bus("separate")) ram_3 (
    .addr(address[2:0]), .din(controlled_buffer_3_out), .data(ram_3_data), .str(or_11_out), .sel(cs),
    .clk(clk), .ld(out), .clr(rst));
  RAM_part #(.addrWidth(3), .dataWidth(32), .bus("separate")) ram_4 (
    .addr(address[2:0]), .din(controlled_buffer_5_out), .data(ram_4_data), .str(or_12_out), .sel(cs),
    .clk(clk), .ld(out), .clr(rst));
  RAM_part #(.addrWidth(3), .dataWidth(32), .bus("separate")) ram_5 (
    .addr(address[2:0]), .din(controlled_buffer_7_out), .data(ram_5_data), .str(or_13_out), .sel(cs),
    .clk(clk), .ld(out), .clr(rst));
  or or_14 (Write_sel, end3, end7, end7);
  Reverser reverser_1 (.Input(ram_2_data), .Output(cpu_output0));
  Reverser reverser_2 (.Input(ram_3_data), .Output(cpu_output1));
  Reverser reverser_3 (.Input(ram_4_data), .Output(cpu_output2));
  Reverser reverser_4 (.Input(ram_5_data), .Output(cpu_output3));
  assign xnor_1_out = ~(address[15:3] ^ storedTAG);  // XNOR_Gate xnor_1, 13 bits wide
  or or_15 (finish, end5, clean_0, clean_1, end2, end3, clean_3, end7, end8, clean_4);
  and and_13 (hit, xnor_1_out[0], xnor_1_out[1], xnor_1_out[2], xnor_1_out[3], xnor_1_out[4], xnor_1_out[5], xnor_1_out[6], xnor_1_out[7], xnor_1_out[8], xnor_1_out[9], xnor_1_out[10], xnor_1_out[11], xnor_1_out[12]);
  Multiplexer #(.enable("false")) multiplexer_8 (.in0(1'b0), .in1(mask[0]), .out(w0), .sel(Write_sel));
  Multiplexer #(.enable("false")) multiplexer_9 (.in0(1'b0), .in1(mask[1]), .out(w1), .sel(Write_sel));
  Multiplexer #(.enable("false")) multiplexer_10 (.in0(1'b0), .in1(mask[2]), .out(w2), .sel(Write_sel));
  Multiplexer #(.enable("false")) multiplexer_11 (.in0(1'b0), .in1(mask[3]), .out(w3), .sel(Write_sel));
  or or_16 (enTag, enTag_0, enTag_1, enTag_4, enTag_2, enTag_3);
  or or_17 (clean, clean_0, clean_1, clean_4, clean_3);
  or or_18 (R_W_OUPUT, enTag_0, enTag_1, enTag_2, enTag_3, enTag_4);
  Multiplexer #(.select(3), .enable("false")) multiplexer_12 (
    .in0(On0), .in1(On1), .in2(On2), .in3(On3), .in4(On4), .in5(On5), .in6(On6), .in7(On7), .out(ON),
    .sel(address[2:0]));
  or or_19 (R_W_INPUT, end3, end7, R_W_INPUT2);
  or or_20 (out, clean_1, clean_0, clean_4, clean_3, end5);
  nor nor_1 (Cond, ON, valid);
  D_Flip_Flop d_ff_1 (.clk(clk), .D(or_21_out), .Q(d_ff_1_q), .preset(rst));  // open: Qn, en, reset
  or or_21 (or_21_out, demultiplexer_1_out0, end2, end3, clean_3, end5, clean_4, end7, end8, clean_0, clean_1);
  D_Flip_Flop d_ff_2 (.clk(clk), .D(clean), .Q(d_ff_2_q), .en(E0), .reset(rst));  // open: Qn, preset
  D_Flip_Flop d_ff_3 (.clk(clk), .D(clean), .Q(d_ff_3_q), .en(E1), .reset(rst));  // open: Qn, preset
  D_Flip_Flop d_ff_4 (.clk(clk), .D(clean), .Q(d_ff_4_q), .en(E2), .reset(rst));  // open: Qn, preset
  D_Flip_Flop d_ff_5 (.clk(clk), .D(clean), .Q(d_ff_5_q), .en(E3), .reset(rst));  // open: Qn, preset
  D_Flip_Flop d_ff_6 (.clk(clk), .D(clean), .Q(d_ff_6_q), .en(E4), .reset(rst));  // open: Qn, preset
  D_Flip_Flop d_ff_7 (.clk(clk), .D(clean), .Q(d_ff_7_q), .en(E5), .reset(rst));  // open: Qn, preset
  D_Flip_Flop d_ff_8 (.clk(clk), .D(clean), .Q(d_ff_8_q), .en(E6), .reset(rst));  // open: Qn, preset
  D_Flip_Flop d_ff_9 (.clk(clk), .D(clean), .Q(d_ff_9_q), .en(E7), .reset(rst));  // open: Qn, preset
  Demultiplexer #(.enable("false")) demultiplexer_1 (
    .out0(demultiplexer_1_out0), .out1(demultiplexer_1_out1), .in(d_ff_1_q), .sel(cs));
  Demultiplexer #(.enable("false")) demultiplexer_2 (
    .out0(demultiplexer_2_out0), .out1(demultiplexer_2_out1), .in(demultiplexer_1_out1), .sel(hit));
  Demultiplexer #(.enable("false")) demultiplexer_3 (
    .out0(demultiplexer_3_out0), .out1(demultiplexer_3_out1), .in(demultiplexer_2_out0), .sel(r_w));
  Multiplexer #(.select(3), .enable("false")) multiplexer_13 (
    .in0(d_ff_2_q), .in1(d_ff_3_q), .in2(d_ff_4_q), .in3(d_ff_5_q), .in4(d_ff_6_q), .in5(d_ff_7_q),
    .in6(d_ff_8_q), .in7(d_ff_9_q), .out(valid), .sel(address[2:0]));
  Demultiplexer #(.enable("false")) demultiplexer_4 (
    .out0(demultiplexer_4_out0), .out1(demultiplexer_4_out1), .in(demultiplexer_3_out1), .sel(Cond));
  Demultiplexer #(.enable("false")) demultiplexer_5 (
    .out0(demultiplexer_5_out0), .out1(demultiplexer_5_out1), .in(demultiplexer_3_out0), .sel(Cond));
  or or_22 (or_22_out, ~valid, valid);  // OR_Gate
  and and_14 (Sel, or_22_out, ON);
  and and_15 (and_15_out, v0, finish);
  and and_16 (and_16_out, v1, finish);
  and and_17 (and_17_out, v2, finish);
  and and_18 (and_18_out, v3, finish);
  and and_19 (and_19_out, v4, finish);
  and and_20 (and_20_out, v5, finish);
  and and_21 (and_21_out, v6, finish);
  and and_22 (and_22_out, v7, finish);
  or or_23 (loadW0, dec0, demultiplexer_5_out0);
  assign controlled_buffer_9_out = not_1_out ? and_15_out : 1'bz;  // Controlled_Buffer controlled_buffer_9
  assign controlled_buffer_10_out = not_2_out ? and_16_out : 1'bz;  // Controlled_Buffer controlled_buffer_10
  assign controlled_buffer_11_out = not_3_out ? and_17_out : 1'bz;  // Controlled_Buffer controlled_buffer_11
  assign controlled_buffer_12_out = not_4_out ? and_18_out : 1'bz;  // Controlled_Buffer controlled_buffer_12
  assign controlled_buffer_13_out = not_5_out ? and_19_out : 1'bz;  // Controlled_Buffer controlled_buffer_13
  assign controlled_buffer_14_out = not_6_out ? and_20_out : 1'bz;  // Controlled_Buffer controlled_buffer_14
  assign controlled_buffer_15_out = not_7_out ? and_21_out : 1'bz;  // Controlled_Buffer controlled_buffer_15
  assign controlled_buffer_16_out = not_8_out ? and_22_out : 1'bz;  // Controlled_Buffer controlled_buffer_16
  D_Flip_Flop d_ff_10 (.clk(clk), .D(loadW0), .Q(RAM_imput_S), .reset(rst));  // open: Qn, preset, en
  or or_24 (loadW2, dec2, demultiplexer_5_out1);
  Demultiplexer #(.enable("false")) demultiplexer_6 (
    .out0(demultiplexer_6_out0), .out1(demultiplexer_6_out1), .in(demultiplexer_2_out1), .sel(r_w));
  not not_1 (not_1_out, On0);
  D_Flip_Flop d_ff_11 (.clk(clk), .D(controlled_buffer_9_out), .Q(On0), .reset(rst));  // open: Qn, preset, en
  D_Flip_Flop d_ff_12 (.clk(clk), .D(controlled_buffer_10_out), .Q(On1), .reset(rst));  // open: Qn, preset, en
  not not_2 (not_2_out, On1);
  D_Flip_Flop d_ff_13 (.clk(clk), .D(controlled_buffer_11_out), .Q(On2), .reset(rst));  // open: Qn, preset, en
  D_Flip_Flop d_ff_14 (.clk(clk), .D(controlled_buffer_12_out), .Q(On3), .reset(rst));  // open: Qn, preset, en
  D_Flip_Flop d_ff_15 (.clk(clk), .D(controlled_buffer_13_out), .Q(On4), .reset(rst));  // open: Qn, preset, en
  D_Flip_Flop d_ff_16 (.clk(clk), .D(controlled_buffer_14_out), .Q(On5), .reset(rst));  // open: Qn, preset, en
  D_Flip_Flop d_ff_17 (.clk(clk), .D(controlled_buffer_15_out), .Q(On6), .reset(rst));  // open: Qn, preset, en
  D_Flip_Flop d_ff_18 (.clk(clk), .D(controlled_buffer_16_out), .Q(On7), .reset(rst));  // open: Qn, preset, en
  D_Flip_Flop d_ff_19 (.clk(clk), .D(loadW2), .Q(ramCS2), .reset(rst));  // open: Qn, preset, en
  or or_25 (loadW3, dec3, demultiplexer_4_out0);
  or or_26 (loadW4, dec4, demultiplexer_4_out1);
  Demultiplexer #(.enable("false")) demultiplexer_7 (
    .out0(demultiplexer_7_out0), .out1(demultiplexer_7_out1), .in(demultiplexer_6_out0), .sel(valid));
  not not_3 (not_3_out, On2);
  not not_4 (not_4_out, On3);
  not not_5 (not_5_out, On4);
  not not_6 (not_6_out, On5);
  not not_7 (not_7_out, On6);
  not not_8 (not_8_out, On7);
  Demultiplexer #(.enable("false")) demultiplexer_8 (
    .out0(dec0), .out1(demultiplexer_8_out1), .in(RAM_imput_S), .sel(finish_t));
  D_Flip_Flop d_ff_20 (.clk(clk), .D(loadW3), .Q(ramCS3), .reset(rst));  // open: Qn, preset, en
  D_Flip_Flop d_ff_21 (.clk(clk), .D(loadW4), .Q(ramCS4), .reset(rst));  // open: Qn, preset, en
  Demultiplexer #(.enable("false")) demultiplexer_9 (
    .out0(demultiplexer_9_out0), .out1(demultiplexer_9_out1), .in(demultiplexer_7_out0), .sel(ON));
  Demultiplexer #(.enable("false")) demultiplexer_10 (.out0(dec2), .out1(enTag_1), .in(ramCS2), .sel(finish_t));
  Demultiplexer #(.enable("false")) demultiplexer_11 (.out0(dec3), .out1(end2), .in(ramCS3), .sel(finish_t));
  Demultiplexer #(.enable("false")) demultiplexer_12 (.out0(dec4), .out1(enTag_2), .in(ramCS4), .sel(finish_t));
  D_Flip_Flop d_ff_22 (.clk(clk), .D(demultiplexer_7_out1), .Q(clean_4));  // open: Qn, preset, en, reset
  Demultiplexer #(.enable("false")) demultiplexer_13 (
    .out0(demultiplexer_13_out0), .out1(R_W_INPUT2), .in(demultiplexer_6_out1), .sel(Sel));
  D_Flip_Flop d_ff_23 (.clk(clk), .D(loadW1), .Q(ramCS1), .reset(rst));  // open: Qn, preset, en
  or or_27 (loadW1, dec1, demultiplexer_8_out1);
  or or_28 (loadW5, dec5, demultiplexer_9_out0);
  D_Flip_Flop d_ff_24 (.clk(clk), .D(loadW5), .Q(ramCS5), .reset(rst));  // open: Qn, preset, en
  D_Flip_Flop d_ff_25 (.clk(clk), .D(demultiplexer_9_out1), .Q(end5));  // open: Qn, preset, en, reset
  Demultiplexer #(.enable("false")) demultiplexer_14 (.out0(dec1), .out1(enTag_0), .in(ramCS1), .sel(finish_t));
  Demultiplexer #(.enable("false")) demultiplexer_15 (.out0(dec5), .out1(enTag_3), .in(ramCS5), .sel(finish_t));
  or or_29 (loadW6, dec6, demultiplexer_13_out0);
  D_Flip_Flop d_ff_26 (.clk(clk), .D(enTag_2), .Q(end3), .reset(rst));  // open: Qn, preset, en
  D_Flip_Flop d_ff_27 (.clk(clk), .D(loadW6), .Q(ramCS6), .reset(rst));  // open: Qn, preset, en
  D_Flip_Flop d_ff_28 (.clk(clk), .D(enTag_1), .Q(clean_1));  // open: Qn, preset, en, reset
  D_Flip_Flop d_ff_29 (.clk(clk), .D(R_W_INPUT2), .Q(end8), .reset(rst));  // open: Qn, preset, en
  Demultiplexer #(.enable("false")) demultiplexer_16 (.out0(dec6), .out1(enTag_4), .in(ramCS6), .sel(finish_t));
  D_Flip_Flop d_ff_30 (.clk(clk), .D(enTag_0), .Q(clean_0), .reset(rst));  // open: Qn, preset, en
  D_Flip_Flop d_ff_31 (.clk(clk), .D(enTag_3), .Q(clean_3), .reset(rst));  // open: Qn, preset, en
  D_Flip_Flop d_ff_32 (.clk(clk), .D(enTag_4), .Q(end7), .reset(rst));  // open: Qn, preset, en

  // Other names for the same wires on the sheet: add[2:0] = address[2:0]; addressToRAM[15:0] = Ram_address;
  //   CPU_INPUT2[31:0] = cpu_input_2; CPU_OUPUT0[31:0] = cpu_output0; CPU_OUPUT1[31:0] = cpu_output1;
  //   CPU_OUPUT2[31:0] = cpu_output2; CPU_OUPUT3[31:0] = cpu_output3; fin2 = end2; fin3 = end3; R_W_INPUT0 = end3;
  //   Write_sel0 = end3; fin7 = end7; R_W_INPUT1 = end7; Write_sel1 = end7; fin8 = end8; final = finish;
  //   load0_0 = enTag_0; load1_0 = enTag_0; load2_0 = enTag_0; load3_0 = enTag_0; R_W_OUPUT0 = enTag_0;
  //   load0_1 = enTag_1; load1_1 = enTag_1; load2_1 = enTag_1; load3_1 = enTag_1; R_W_OUPUT1 = enTag_1;
  //   load0_2 = enTag_2; load1_2 = enTag_2; load2_2 = enTag_2; load3_2 = enTag_2; R_W_OUPUT4 = enTag_2;
  //   load0_3 = enTag_3; load1_3 = enTag_3; load2_3 = enTag_3; load3_3 = enTag_3; R_W_OUPUT2 = enTag_3;
  //   load0_4 = enTag_4; load1_4 = enTag_4; load2_4 = enTag_4; load3_4 = enTag_4; R_W_OUPUT3 = enTag_4;
  //   Stime_0 = loadW0; Stime_1 = loadW3; Bank0 = mask[0]; Bank1 = mask[1]; Bank2 = mask[2]; Bank3 = mask[3];
  //   end1 = clean_1; fin1 = clean_1; out_0 = clean_1; end0 = clean_0; fin0 = clean_0; out_1 = clean_0;
  //   end4 = clean_3; fin4 = clean_3; out_2 = clean_3; fin5 = end5; out_3 = end5; end6 = clean_4; fin6 = clean_4;
  //   out_4 = clean_4; RAM_OUPUT0[31:0] = ram_output0; RAM_OUPUT1[31:0] = ram_output1; RAM_OUPUT2[31:0] = ram_output2;
  //   RAM_OUPUT3[31:0] = ram_output3; ramCS = rsmCS; ramCS0 = RAM_imput_S; ramR_W0 = RAM_imput_S;
  //   S_mask = RAM_imput_S; Saddr = RAM_imput_S; ramR_W1 = ramCS3; TAG[12:0] = address[15:3]; Write_sel2 = R_W_INPUT2
endmodule

module HILO (
  input  reset,
  input  R_W,
  input  Selector,
  input  [31:0] HI,
  input  [31:0] LO,
  input  clk,
  output [31:0] HI_LO
);

  wire not_1_out;
  wire [31:0] HI_q, LO_q;

  Register #(.width(32), .trigger("falling")) u_HI (.D(HI), .en(R_W), .Q(HI_q), .clk(clk), .clr(reset));
  Multiplexer #(.width(32), .disabled(0), .enable("false")) multiplexer_1 (
    .in0(HI_q), .in1(LO_q), .out(HI_LO), .sel(not_1_out));
  Register #(.width(32), .trigger("falling")) u_LO (.D(LO), .en(R_W), .Q(LO_q), .clk(clk), .clr(reset));
  not not_1 (not_1_out, Selector);
endmodule

module Reverser (
  input  [31:0] Input,
  output [31:0] Output
);

  // Probe on {Input[7:0], Input[15:8], Input[23:16], Input[31:24]}

  assign Output = {Input[7:0], Input[15:8], Input[23:16], Input[31:24]};

  // Other names for the same wires on the sheet: _3[7:0] = Input[31:24]; in[31:0] = Input;
  //   out[31:0] = {Input[7:0], Input[15:8], Input[23:16], Input[31:24]}; _2[7:0] = Input[23:16];
  //   _1[7:0] = Input[15:8]
endmodule

module DataPath (
  input  Clock,
  input  Reset,
  input  [31:0] Input,
  input  IorD,
  input  [1:0] RegDst,
  input  [1:0] RegWriteSelector,
  input  [1:0] ALUSrcA,
  input  [1:0] ALUSrcB,
  input  Branch,
  input  PCWrite,
  input  RegWrite,
  input  [1:0] PCSrc,
  input  [5:0] ALUControl,
  input  IRWrite,
  input  ExtOp,
  input  HiLo_RW,
  input  HiLo_Selector,
  input  OutA,
  output [31:0] MemOutput,
  output [31:0] MemOutputAddress,
  output [5:0] FuncCode,
  output [5:0] OpCode
);

  wire alu_1_equals, alu_1_greater, alu_1_less, alu_1_overflow, and_1_out, branchcontrol_1_condition, PCEn;
  wire [4:0] multiplexer_2_out, RD, RS, RT, X;
  wire [15:0] shamnt;
  wire [27:0] PC;
  wire [31:0] A, Addrr, alu_1_hi, alu_1_lo, alu_1_output, ALUOut, B, Data, extended, HiLo, Jump,
       multiplexer_4_out, multiplexer_5_out, multiplexer_6_out, PCIn, Random, registerfile_1_read_data_1,
       registerfile_1_read_data_2, shifted_left, SP;
  wire [31:28] shifter_2_out;

  Random #(.width(32)) random_1 (.clk(Clock), .out(Random));  // open: next, clr
  // Probe on Input
  InstructionRegister instructionregister_1 (
    .Instruction(Input), .Funct_code(FuncCode), .X(X), .Rd(RD), .Rt(RT), .Rs(RS), .Op_code(OpCode),
    .Enable(IRWrite), .CLK(Clock), .Clear(Reset), .shamnt(shamnt), .Instruction_2(Addrr));
  Register #(.width(32)) DataReg (.D(Input), .en(1'b1), .Q(Data), .clk(Clock), .clr(Reset));
  Register #(.width(32)) u_PC (.D(PCIn), .en(PCEn), .Q({Jump[31:28], PC}), .clk(Clock), .clr(Reset));
  Multiplexer #(.width(32), .enable("false")) multiplexer_1 (.in0(B), .in1(A), .out(MemOutput), .sel(OutA));
  // Probe on Data
  // Probe on {Jump[31:28], PC}
  Extender extender_1 (.Input(shamnt), .ExtOp(ExtOp), .out_3(extended));
  // Probe on shamnt
  // Probe on RS
  // Probe on RT
  Multiplexer #(.select(2), .width(5), .enable("false")) multiplexer_2 (
    .in0(RT), .in1(RD), .in2({5{1'b1}}), .out(multiplexer_2_out), .sel(RegDst));  // open: in3
  // Probe on multiplexer_2_out
  Multiplexer #(.width(32), .enable("false")) multiplexer_3 (
    .in0({Jump[31:28], PC}), .in1(ALUOut), .out(MemOutputAddress), .sel(IorD));
  Multiplexer #(.select(2), .width(32), .enable("false")) multiplexer_4 (
    .in0(ALUOut), .in1(Data), .in2(HiLo), .in3(Random), .out(multiplexer_4_out), .sel(RegWriteSelector));
  // Probe on extended
  Shifter #(.width(32)) shifter_1 (.in(extended), .\dist (5'b00010), .out(shifted_left));
  Shifter #(.width(32)) shifter_2 (.in(Addrr), .\dist (5'b00010), .out({shifter_2_out, Jump[27:0]}));
  Register #(.width(32)) register_1 (.D(registerfile_1_read_data_1), .en(1'b1), .Q(A), .clk(Clock), .clr(Reset));
  RegisterFile registerfile_1 (
    .\Dirección_de_destino (multiplexer_2_out), .Read_Write(RegWrite), .Datos_de_entrada(multiplexer_4_out),
    .Selector_de_salida_A(RS), .Selector_de_salida_B(RT), .Reset(Reset), .Clock(Clock),
    .Read_Data_1(registerfile_1_read_data_1), .Read_Data_2(registerfile_1_read_data_2), .SP(SP));
  Register #(.width(32)) register_2 (.D(registerfile_1_read_data_2), .en(1'b1), .Q(B), .clk(Clock), .clr(Reset));
  // Probe on multiplexer_4_out
  // Probe on multiplexer_5_out
  Multiplexer #(.select(2), .width(32), .enable("false")) multiplexer_5 (
    .in0(B), .in1(32'h4), .in2(extended), .in3(shifted_left), .out(multiplexer_5_out), .sel(ALUSrcB));
  ALU alu_1 (
    .Op1(multiplexer_6_out), .Op2(multiplexer_5_out), .Instruction(ALUControl), .HI(alu_1_hi), .LO(alu_1_lo),
    .Output(alu_1_output), .Overflow(alu_1_overflow), .Greater(alu_1_greater), .Equals(alu_1_equals),
    .Less(alu_1_less));  // open: Carry, Zero
  Multiplexer #(.select(2), .width(32), .enable("false")) multiplexer_6 (
    .in0({Jump[31:28], PC}), .in1(A), .in2(SP), .out(multiplexer_6_out), .sel(ALUSrcA));  // open: in3
  Register #(.width(32)) u_AluOut (.D(alu_1_output), .en(1'b1), .Q(ALUOut), .clk(Clock), .clr(Reset));
  Multiplexer #(.select(2), .width(32), .enable("false")) multiplexer_7 (
    .in0(alu_1_output), .in1(ALUOut), .in2(Jump), .in3(A), .out(PCIn), .sel(PCSrc));
  HILO hilo_1 (
    .reset(Reset), .R_W(HiLo_RW), .Selector(HiLo_Selector), .HI(alu_1_hi), .LO(alu_1_lo), .HI_LO(HiLo),
    .clk(Clock));
  // Probe on multiplexer_6_out
  // Probe on ALUOut
  BranchControl branchcontrol_1 (
    .Zero(alu_1_overflow), .Less(alu_1_less), .Greater(alu_1_greater), .Equals(alu_1_equals),
    .BranchFunction(OpCode), .Condition(branchcontrol_1_condition));
  and and_1 (and_1_out, Branch, branchcontrol_1_condition);
  or or_1 (PCEn, PCWrite, and_1_out);

  // Other names for the same wires on the sheet: CLK = Clock; Func_C[5:0] = FuncCode; PC[31:28] = Jump[31:28];
  //   MemInput[31:0] = Input; MemOutputData[31:0] = MemOutput; Op_C[5:0] = OpCode

  // Notes on the sheet:
  //   INPUTS
  //   Control Flags
  //   Random Generator
  //   Decoded Instr
endmodule

module MemoryInputSelector (
  input  [31:0] Address,
  output [3:0] Mask,
  output [15:0] Address_2
);

  wire not_1_out, not_2_out, not_3_out, not_4_out;

  not not_1 (not_1_out, Address[3]);
  not not_2 (not_2_out, Address[2]);
  not not_3 (not_3_out, Address[3]);
  not not_4 (not_4_out, Address[2]);
  and and_1 (Mask[3], Address[3], Address[2]);
  and and_2 (Mask[0], not_1_out, not_2_out);
  and and_3 (Mask[1], not_3_out, Address[2]);
  and and_4 (Mask[2], Address[3], not_4_out);

  assign Address_2 = Address[19:4];
endmodule

module MemoryOutputSelection (
  input  [31:0] Address,
  input  [31:0] Input_0,
  input  [31:0] Input_1,
  input  [31:0] Input_2,
  input  [31:0] Input_3,
  output [31:0] Output
);

  wire and_1_out, and_2_out, and_3_out, and_4_out, not_1_out, not_2_out, not_3_out, not_4_out;

  not not_1 (not_1_out, Address[3]);
  not not_2 (not_2_out, Address[2]);
  not not_3 (not_3_out, Address[3]);
  not not_4 (not_4_out, Address[2]);
  and and_1 (and_1_out, Address[3], Address[2]);
  and and_2 (and_2_out, not_1_out, not_2_out);
  and and_3 (and_3_out, not_3_out, Address[2]);
  and and_4 (and_4_out, Address[3], not_4_out);
  assign Output = and_2_out ? Input_0 : 32'bz;  // Controlled_Buffer controlled_buffer_1
  assign Output = and_3_out ? Input_1 : 32'bz;  // Controlled_Buffer controlled_buffer_2
  assign Output = and_4_out ? Input_2 : 32'bz;  // Controlled_Buffer controlled_buffer_3
  assign Output = and_1_out ? Input_3 : 32'bz;  // Controlled_Buffer controlled_buffer_4
endmodule
